// Logisim project study.circ as structural Verilog: 30 circuits, main circuit main
module main (
  input  [3:0] A,
  input  Cin,
  input  [3:0] B,
  input  in_4,
  input  [7:0] in_5,
  input  [7:0] in_6,
  output [3:0] S,
  output Cout,
  output overflow,
  output [7:0] out_10,
  output out_11
);

  wire fa_1_cout, fa_2_cout, fa_3_cout;

  Adder adder_1 (.a(in_5), .b(in_6), .out(out_10), .cin(in_4), .cout(out_11));
  FA fa_1 (.A(A[0]), .Cin(Cin), .B(B[0]), .S(S[0]), .Cout(fa_1_cout));
  FA fa_2 (.A(A[1]), .Cin(fa_1_cout), .B(B[1]), .S(S[1]), .Cout(fa_2_cout));
  FA fa_3 (.A(A[2]), .Cin(fa_2_cout), .B(B[2]), .S(S[2]), .Cout(fa_3_cout));
  FA fa_4 (.A(A[3]), .Cin(fa_3_cout), .B(B[3]), .S(S[3]), .Cout(Cout));
  xor xor_1 (overflow, Cout, fa_3_cout);

  // Notes on the sheet:
  //   in_5: initial=0x6
  //   -2 + -4不溢出 1110+1100=11010
  //   4 + 5 溢出0100+0101=1001
endmodule

module myOR (
  input  in_1,
  input  in_2,
  output out_3
);

  wire transistor_1_out, transistor_2_out;

  Transistor #(.\type ("n")) transistor_1 (.in(1'b0), .out(transistor_1_out), .gate(in_1));
  Transistor transistor_2 (.in(1'b1), .out(transistor_2_out), .gate(in_1));
  Transistor transistor_3 (.in(transistor_2_out), .out(transistor_1_out), .gate(in_2));
  Transistor #(.\type ("n")) transistor_4 (.in(1'b0), .out(transistor_1_out), .gate(in_2));
  Transistor transistor_5 (.in(1'b1), .out(out_3), .gate(transistor_1_out));
  Transistor #(.\type ("n")) transistor_6 (.in(1'b0), .out(out_3), .gate(transistor_1_out));
endmodule

module MyDecoder3To8 (
  input  [2:0] in_1,
  output Out_8,
  output Out_7,
  output Out_6,
  output Out_5,
  output Out_4,
  output Out_3,
  output Out_2,
  output Out_1
);

  wire mydecoder2to4_1_out_2, mydecoder2to4_1_out_3, mydecoder2to4_1_out_4, mydecoder2to4_1_out_5,
       mydecoder2to4_2_out_2, mydecoder2to4_2_out_3, mydecoder2to4_2_out_4, mydecoder2to4_2_out_5, not_1_out;

  not not_1 (not_1_out, in_1[2]);
  MyDecoder2To4 mydecoder2to4_1 (
    .in_1(in_1[1:0]), .out_2(mydecoder2to4_1_out_2), .out_3(mydecoder2to4_1_out_3),
    .out_4(mydecoder2to4_1_out_4), .out_5(mydecoder2to4_1_out_5));
  MyDecoder2To4 mydecoder2to4_2 (
    .in_1(in_1[1:0]), .out_2(mydecoder2to4_2_out_2), .out_3(mydecoder2to4_2_out_3),
    .out_4(mydecoder2to4_2_out_4), .out_5(mydecoder2to4_2_out_5));
  and and_1 (Out_8, not_1_out, mydecoder2to4_1_out_2);
  and and_2 (Out_7, not_1_out, mydecoder2to4_1_out_3);
  and and_3 (Out_5, mydecoder2to4_1_out_5, not_1_out);
  and and_4 (Out_4, in_1[2], mydecoder2to4_2_out_2);
  and and_5 (Out_3, in_1[2], mydecoder2to4_2_out_3);
  and and_6 (Out_2, mydecoder2to4_2_out_4, in_1[2]);
  and and_7 (Out_1, mydecoder2to4_2_out_5, in_1[2]);
  and and_8 (Out_6, mydecoder2to4_1_out_4, not_1_out);
endmodule

module MyDecoder2To4 (
  input  [1:0] in_1,
  output out_2,
  output out_3,
  output out_4,
  output out_5
);

  wire xor_1_out;

  and and_1 (out_5, in_1[0], in_1[1]);
  nor nor_1 (out_2, in_1[0], in_1[1]);
  xor xor_1 (xor_1_out, in_1[0], in_1[1]);
  and and_2 (out_3, in_1[0], xor_1_out);
  and and_3 (out_4, xor_1_out, in_1[1]);
endmodule

module MyDecoder4To16 (
  input  [3:0] in_1,
  input  in_2,
  output out_3,
  output out_4,
  output out_5,
  output out_6,
  output out_7,
  output out_8,
  output out_9,
  output out_10,
  output out_11,
  output out_12,
  output out_13,
  output out_14,
  output out_15,
  output out_16,
  output out_17,
  output out_18
);

  wire mydecoder3to8_1_out_1, mydecoder3to8_1_out_2, mydecoder3to8_1_out_3, mydecoder3to8_1_out_4,
       mydecoder3to8_1_out_5, mydecoder3to8_1_out_6, mydecoder3to8_1_out_7, mydecoder3to8_1_out_8,
       mydecoder3to8_2_out_1, mydecoder3to8_2_out_2, mydecoder3to8_2_out_3, mydecoder3to8_2_out_4,
       mydecoder3to8_2_out_5, mydecoder3to8_2_out_6, mydecoder3to8_2_out_7, mydecoder3to8_2_out_8, not_1_out;

  not not_1 (not_1_out, in_1[3]);
  MyDecoder3To8 mydecoder3to8_1 (
    .in_1(in_1[2:0]), .Out_8(mydecoder3to8_1_out_8), .Out_7(mydecoder3to8_1_out_7),
    .Out_6(mydecoder3to8_1_out_6), .Out_5(mydecoder3to8_1_out_5), .Out_4(mydecoder3to8_1_out_4),
    .Out_3(mydecoder3to8_1_out_3), .Out_2(mydecoder3to8_1_out_2), .Out_1(mydecoder3to8_1_out_1));
  MyDecoder3To8 mydecoder3to8_2 (
    .in_1(in_1[2:0]), .Out_8(mydecoder3to8_2_out_8), .Out_7(mydecoder3to8_2_out_7),
    .Out_6(mydecoder3to8_2_out_6), .Out_5(mydecoder3to8_2_out_5), .Out_4(mydecoder3to8_2_out_4),
    .Out_3(mydecoder3to8_2_out_3), .Out_2(mydecoder3to8_2_out_2), .Out_1(mydecoder3to8_2_out_1));
  and and_1 (out_3, mydecoder3to8_1_out_8, in_2, not_1_out);
  and and_2 (out_4, mydecoder3to8_1_out_7, in_2, not_1_out);
  and and_3 (out_5, mydecoder3to8_1_out_6, in_2, not_1_out);
  and and_4 (out_6, mydecoder3to8_1_out_5, in_2, not_1_out);
  and and_5 (out_7, mydecoder3to8_1_out_4, in_2, not_1_out);
  and and_6 (out_8, mydecoder3to8_1_out_3, in_2, not_1_out);
  and and_7 (out_9, mydecoder3to8_1_out_2, in_2, not_1_out);
  and and_8 (out_10, mydecoder3to8_1_out_1, in_2, not_1_out);
  and and_9 (out_11, mydecoder3to8_2_out_8, in_2, in_1[3]);
  and and_10 (out_12, mydecoder3to8_2_out_7, in_2, in_1[3]);
  and and_11 (out_13, mydecoder3to8_2_out_6, in_2, in_1[3]);
  and and_12 (out_14, mydecoder3to8_2_out_5, in_2, in_1[3]);
  and and_13 (out_15, mydecoder3to8_2_out_4, in_2, in_1[3]);
  and and_14 (out_16, mydecoder3to8_2_out_3, in_2, in_1[3]);
  and and_15 (out_17, mydecoder3to8_2_out_2, in_2, in_1[3]);
  and and_16 (out_18, mydecoder3to8_2_out_1, in_2, in_1[3]);
endmodule

module MyPriorityEncoder4To2 (
  input  A3,
  input  A2,
  input  A1,
  input  A0,
  output Y1,
  output Y0
);

  wire and_1_out, not_1_out;

  not not_1 (not_1_out, A2);
  and and_1 (and_1_out, not_1_out, A1);
  or or_1 (Y1, A3, A2);
  or or_2 (Y0, and_1_out, A3);
endmodule

module MyEncoder4To2 (
  input  A3,
  input  A2,
  input  A1,
  input  A0,
  output Y1,
  output Y0
);

  or or_1 (Y1, A3, A2);
  or or_2 (Y0, A3, A1);
endmodule

module Chiocer3Bit4To1 (
  input  [1:0] in_1,
  input  [2:0] in_2,
  input  [2:0] in_3,
  input  [2:0] in_4,
  input  [2:0] in_5,
  output [2:0] out_6
);

  wire [2:0] and_1_out, and_2_out, and_3_out, and_4_out;
  wire [2:2] mydecoder2to4_1_out_2, mydecoder2to4_1_out_3, mydecoder2to4_1_out_4, mydecoder2to4_1_out_5;

  MyDecoder2To4 mydecoder2to4_1 (
    .in_1(in_1), .out_2(mydecoder2to4_1_out_2[2]), .out_3(mydecoder2to4_1_out_3[2]),
    .out_4(mydecoder2to4_1_out_4[2]), .out_5(mydecoder2to4_1_out_5[2]));
  assign and_1_out = in_2 & {3{mydecoder2to4_1_out_2[2]}};  // AND_Gate and_1, 3 bits wide
  assign and_2_out = in_3 & {3{mydecoder2to4_1_out_3[2]}};  // AND_Gate and_2, 3 bits wide
  assign and_3_out = in_4 & {3{mydecoder2to4_1_out_4[2]}};  // AND_Gate and_3, 3 bits wide
  assign and_4_out = in_5 & {3{mydecoder2to4_1_out_5[2]}};  // AND_Gate and_4, 3 bits wide
  assign out_6 = and_1_out | and_2_out | and_3_out | and_4_out;  // OR_Gate or_1, 3 bits wide
endmodule

module HA (
  input  A,
  input  B,
  output S,
  output C
);

  xor xor_1 (S, A, B);
  and and_1 (C, A, B);
endmodule

module FA (
  input  A,
  input  Cin,
  input  B,
  output S,
  output Cout
);

  wire and_1_out, and_2_out, xor_1_out;

  and and_1 (and_1_out, A, Cin);
  xor xor_1 (xor_1_out, A, Cin);
  xor xor_2 (S, xor_1_out, B);
  and and_2 (and_2_out, xor_1_out, B);
  or or_1 (Cout, and_1_out, and_2_out);
endmodule

module My7SegmentDecoder0 (
  input  [3:0] In_1,
  input  in_2,
  output G,
  output F,
  output A,
  output B,
  output E,
  output D,
  output C,
  output point
);

  wire mydecoder4to16_1_out_3, mydecoder4to16_1_out_4, mydecoder4to16_1_out_5, mydecoder4to16_1_out_6,
       mydecoder4to16_1_out_7, mydecoder4to16_1_out_8, mydecoder4to16_1_out_9, mydecoder4to16_1_out_10,
       mydecoder4to16_1_out_11, mydecoder4to16_1_out_12, mydecoder4to16_1_out_13, mydecoder4to16_1_out_14,
       mydecoder4to16_1_out_15, mydecoder4to16_1_out_16, mydecoder4to16_1_out_17, mydecoder4to16_1_out_18;

  MyDecoder4To16 mydecoder4to16_1 (
    .in_1(In_1), .in_2(in_2), .out_3(mydecoder4to16_1_out_3), .out_4(mydecoder4to16_1_out_4),
    .out_5(mydecoder4to16_1_out_5), .out_6(mydecoder4to16_1_out_6), .out_7(mydecoder4to16_1_out_7),
    .out_8(mydecoder4to16_1_out_8), .out_9(mydecoder4to16_1_out_9), .out_10(mydecoder4to16_1_out_10),
    .out_11(mydecoder4to16_1_out_11), .out_12(mydecoder4to16_1_out_12), .out_13(mydecoder4to16_1_out_13),
    .out_14(mydecoder4to16_1_out_14), .out_15(mydecoder4to16_1_out_15), .out_16(mydecoder4to16_1_out_16),
    .out_17(mydecoder4to16_1_out_17), .out_18(mydecoder4to16_1_out_18));
  or or_1 (A, mydecoder4to16_1_out_3, mydecoder4to16_1_out_5, mydecoder4to16_1_out_6, mydecoder4to16_1_out_8, mydecoder4to16_1_out_9, mydecoder4to16_1_out_10, mydecoder4to16_1_out_11, mydecoder4to16_1_out_12);
  or or_2 (B, mydecoder4to16_1_out_3, mydecoder4to16_1_out_4, mydecoder4to16_1_out_5, mydecoder4to16_1_out_6, mydecoder4to16_1_out_7, mydecoder4to16_1_out_10, mydecoder4to16_1_out_11, mydecoder4to16_1_out_12);
  or or_3 (C, mydecoder4to16_1_out_3, mydecoder4to16_1_out_4, mydecoder4to16_1_out_6, mydecoder4to16_1_out_7, mydecoder4to16_1_out_8, mydecoder4to16_1_out_9, mydecoder4to16_1_out_10, mydecoder4to16_1_out_11, mydecoder4to16_1_out_12);
  or or_4 (D, mydecoder4to16_1_out_3, mydecoder4to16_1_out_5, mydecoder4to16_1_out_6, mydecoder4to16_1_out_8, mydecoder4to16_1_out_9, mydecoder4to16_1_out_11, mydecoder4to16_1_out_12);
  or or_5 (E, mydecoder4to16_1_out_3, mydecoder4to16_1_out_5, mydecoder4to16_1_out_9, mydecoder4to16_1_out_11);
  or or_6 (F, mydecoder4to16_1_out_3, mydecoder4to16_1_out_7, mydecoder4to16_1_out_8, mydecoder4to16_1_out_9, mydecoder4to16_1_out_11, mydecoder4to16_1_out_12);
  or or_7 (G, mydecoder4to16_1_out_5, mydecoder4to16_1_out_6, mydecoder4to16_1_out_7, mydecoder4to16_1_out_8, mydecoder4to16_1_out_9, mydecoder4to16_1_out_11, mydecoder4to16_1_out_12);
  or or_8 (point, mydecoder4to16_1_out_13, mydecoder4to16_1_out_14, mydecoder4to16_1_out_15, mydecoder4to16_1_out_16, mydecoder4to16_1_out_17, mydecoder4to16_1_out_18);
endmodule

module My7SegmentDecoder (
  input  [3:0] In_1,
  input  in_2,
  output G,
  output F,
  output A,
  output B,
  output E,
  output D,
  output C
);

  wire mydecoder4to16_1_out_3, mydecoder4to16_1_out_4, mydecoder4to16_1_out_5, mydecoder4to16_1_out_6,
       mydecoder4to16_1_out_7, mydecoder4to16_1_out_8, mydecoder4to16_1_out_9, mydecoder4to16_1_out_10,
       mydecoder4to16_1_out_11, mydecoder4to16_1_out_12, mydecoder4to16_1_out_13, mydecoder4to16_1_out_14,
       mydecoder4to16_1_out_15, mydecoder4to16_1_out_16, mydecoder4to16_1_out_17, mydecoder4to16_1_out_18,
       or_1_out, or_8_out;

  MyDecoder4To16 mydecoder4to16_1 (
    .in_1(In_1), .in_2(in_2), .out_3(mydecoder4to16_1_out_3), .out_4(mydecoder4to16_1_out_4),
    .out_5(mydecoder4to16_1_out_5), .out_6(mydecoder4to16_1_out_6), .out_7(mydecoder4to16_1_out_7),
    .out_8(mydecoder4to16_1_out_8), .out_9(mydecoder4to16_1_out_9), .out_10(mydecoder4to16_1_out_10),
    .out_11(mydecoder4to16_1_out_11), .out_12(mydecoder4to16_1_out_12), .out_13(mydecoder4to16_1_out_13),
    .out_14(mydecoder4to16_1_out_14), .out_15(mydecoder4to16_1_out_15), .out_16(mydecoder4to16_1_out_16),
    .out_17(mydecoder4to16_1_out_17), .out_18(mydecoder4to16_1_out_18));
  or or_1 (or_1_out, mydecoder4to16_1_out_3, mydecoder4to16_1_out_4, mydecoder4to16_1_out_5, mydecoder4to16_1_out_6, mydecoder4to16_1_out_7, mydecoder4to16_1_out_10, mydecoder4to16_1_out_11, mydecoder4to16_1_out_12);
  or or_2 (D, mydecoder4to16_1_out_14, mydecoder4to16_1_out_3, mydecoder4to16_1_out_5, mydecoder4to16_1_out_6, mydecoder4to16_1_out_8, mydecoder4to16_1_out_15, mydecoder4to16_1_out_9, mydecoder4to16_1_out_11, mydecoder4to16_1_out_12, mydecoder4to16_1_out_16, mydecoder4to16_1_out_17);
  or or_3 (C, mydecoder4to16_1_out_13, mydecoder4to16_1_out_14, mydecoder4to16_1_out_3, mydecoder4to16_1_out_4, mydecoder4to16_1_out_6, mydecoder4to16_1_out_7, mydecoder4to16_1_out_8, mydecoder4to16_1_out_9, mydecoder4to16_1_out_10, mydecoder4to16_1_out_11, mydecoder4to16_1_out_16, mydecoder4to16_1_out_12);
  or or_4 (F, mydecoder4to16_1_out_13, mydecoder4to16_1_out_3, mydecoder4to16_1_out_7, mydecoder4to16_1_out_8, mydecoder4to16_1_out_9, mydecoder4to16_1_out_14, mydecoder4to16_1_out_11, mydecoder4to16_1_out_12, mydecoder4to16_1_out_15, mydecoder4to16_1_out_17, mydecoder4to16_1_out_18);
  or or_5 (G, mydecoder4to16_1_out_8, mydecoder4to16_1_out_13, mydecoder4to16_1_out_14, mydecoder4to16_1_out_5, mydecoder4to16_1_out_6, mydecoder4to16_1_out_7, mydecoder4to16_1_out_9, mydecoder4to16_1_out_11, mydecoder4to16_1_out_12, mydecoder4to16_1_out_16, mydecoder4to16_1_out_17, mydecoder4to16_1_out_18);
  or or_6 (A, mydecoder4to16_1_out_13, mydecoder4to16_1_out_15, mydecoder4to16_1_out_3, mydecoder4to16_1_out_5, mydecoder4to16_1_out_6, mydecoder4to16_1_out_8, mydecoder4to16_1_out_9, mydecoder4to16_1_out_10, mydecoder4to16_1_out_11, mydecoder4to16_1_out_12, mydecoder4to16_1_out_17, mydecoder4to16_1_out_18);
  or or_7 (E, mydecoder4to16_1_out_13, mydecoder4to16_1_out_3, mydecoder4to16_1_out_5, mydecoder4to16_1_out_9, mydecoder4to16_1_out_11, mydecoder4to16_1_out_14, mydecoder4to16_1_out_15, mydecoder4to16_1_out_16, mydecoder4to16_1_out_17, mydecoder4to16_1_out_18);
  or or_8 (or_8_out, mydecoder4to16_1_out_13, mydecoder4to16_1_out_16);
  or or_9 (B, or_1_out, or_8_out);
endmodule

module FS (
  input  A,
  input  Bin,
  input  B,
  output D,
  output Bout
);

  wire and_1_out, and_2_out, and_3_out, not_1_out, xor_1_out;

  not not_1 (not_1_out, A);
  and and_1 (and_1_out, Bin, not_1_out);
  xor xor_1 (xor_1_out, A, Bin);
  and and_2 (and_2_out, not_1_out, B);
  xor xor_2 (D, xor_1_out, B);
  and and_3 (and_3_out, Bin, B);
  or or_1 (Bout, and_1_out, and_3_out, and_2_out);
endmodule

module DLatch (
  input  WE,
  input  D,
  input  in_3,
  output Q
);

  wire and_1_out, and_2_out, and_3_out, nor_1_out, not_1_out, not_2_out, or_1_out;

  not not_1 (not_1_out, in_3);
  and and_1 (and_1_out, WE, not_1_out);
  not not_2 (not_2_out, D);
  and and_2 (and_2_out, D, and_1_out);
  and and_3 (and_3_out, and_1_out, not_2_out);
  nor nor_1 (nor_1_out, and_2_out, Q);
  nor nor_2 (Q, nor_1_out, or_1_out);
  or or_1 (or_1_out, and_3_out, in_3);
endmodule

module DFlipFlop (
  input  D,
  input  EN,
  input  CLK,
  input  R,
  output Q
);

  wire and_1_out, and_2_out, nand_1_out, nand_2_out, nand_3_out, nand_4_out, nand_5_out, not_1_out,
       not_2_out, or_1_out;

  and and_1 (and_1_out, Q, not_1_out);
  not not_1 (not_1_out, EN);
  or or_1 (or_1_out, and_1_out, and_2_out);
  and and_2 (and_2_out, EN, D);
  nand nand_1 (nand_1_out, not_2_out, or_1_out, nand_2_out);
  nand nand_2 (nand_2_out, nand_1_out, CLK, nand_3_out);
  nand nand_3 (nand_3_out, not_2_out, CLK, nand_4_out);
  nand nand_4 (nand_4_out, nand_3_out, nand_1_out);
  nand nand_5 (nand_5_out, not_2_out, nand_2_out, Q);
  nand nand_6 (Q, nand_5_out, nand_3_out);
  not not_2 (not_2_out, R);
endmodule

module DFlipFlop0 (
  input  D,
  input  EN,
  input  CLK,
  input  R,
  input  in_5,
  input  in_6,
  input  in_7,
  input  in_8,
  output Q,
  output out_10,
  output out_11
);

  wire and_1_out, and_2_out, G2_out, G3_out, G4_out, G5_out, G6_out, nand_2_out, nor_2_out, not_1_out,
       not_2_out, or_1_out;

  not not_1 (not_1_out, EN);
  and and_1 (and_1_out, Q, not_1_out);
  or or_1 (or_1_out, and_1_out, and_2_out);
  and and_2 (and_2_out, EN, D);
  nand G6 (G6_out, not_2_out, or_1_out, G4_out);
  nand G4 (G4_out, G6_out, CLK, G3_out);
  nand G3 (G3_out, not_2_out, CLK, G5_out);
  nand G5 (G5_out, G3_out, G6_out);
  nand G2 (G2_out, not_2_out, G4_out, Q);
  not not_2 (not_2_out, R);
  nand G1 (Q, G2_out, G3_out);
  nor nor_1 (out_10, in_5, nor_2_out);
  nor nor_2 (nor_2_out, out_10, in_6);
  nand nand_1 (out_11, in_7, nand_2_out);
  nand nand_2 (nand_2_out, out_11, in_8);
endmodule

module MyClock (
);

  wire and_3_out, and_4_out, and_6_out, b1, b2, b3, b4, button_1_out, clock_1_out, my7segmentdecoder_1_a,
       my7segmentdecoder_1_b, my7segmentdecoder_1_c, my7segmentdecoder_1_d, my7segmentdecoder_1_e,
       my7segmentdecoder_1_f, my7segmentdecoder_1_g, my7segmentdecoder_2_a, my7segmentdecoder_2_b,
       my7segmentdecoder_2_c, my7segmentdecoder_2_d, my7segmentdecoder_2_e, my7segmentdecoder_2_f,
       my7segmentdecoder_2_g, my7segmentdecoder_3_a, my7segmentdecoder_3_b, my7segmentdecoder_3_c,
       my7segmentdecoder_3_d, my7segmentdecoder_3_e, my7segmentdecoder_3_f, my7segmentdecoder_3_g,
       my7segmentdecoder_4_a, my7segmentdecoder_4_b, my7segmentdecoder_4_c, my7segmentdecoder_4_d,
       my7segmentdecoder_4_e, my7segmentdecoder_4_f, my7segmentdecoder_4_g, or_1_out, or_2_out, or_3_out,
       or_4_out, xnor_1_out, xnor_2_out, xnor_3_out, xnor_4_out, xnor_5_out, xnor_6_out, xnor_7_out,
       xnor_8_out, xnor_9_out, xnor_10_out, xnor_11_out, xnor_12_out, xnor_13_out, xnor_14_out, xnor_15_out,
       xnor_16_out;
  wire [3:0] a1, a2, a3, a4, fa4_1_s, fa4_2_s, fa4_3_s, fa4_4_s;

  FA4 fa4_1 (.A(4'b0001), .B(a1), .S(fa4_1_s));  // open: Cin, Cout
  Clock clock_1 (.out(clock_1_out));
  xnor xnor_1 (xnor_1_out, a1[0], 1'b0);
  xnor xnor_2 (xnor_2_out, a1[1], 1'b1);
  xnor xnor_3 (xnor_3_out, a1[2], 1'b0);
  xnor xnor_4 (xnor_4_out, a1[3], 1'b1);
  Button button_1 (.out(button_1_out));
  or or_1 (or_1_out, button_1_out, b1);
  and and_1 (b1, xnor_1_out, xnor_2_out, xnor_3_out, xnor_4_out);
  DFlipFlop dflipflop_1 (.D(fa4_1_s[0]), .EN(1'b1), .CLK(clock_1_out), .R(or_1_out), .Q(a1[0]));
  DFlipFlop dflipflop_2 (.D(fa4_1_s[1]), .EN(1'b1), .CLK(clock_1_out), .R(or_1_out), .Q(a1[1]));
  DFlipFlop dflipflop_3 (.D(fa4_1_s[2]), .EN(1'b1), .CLK(clock_1_out), .R(or_1_out), .Q(a1[2]));
  DFlipFlop dflipflop_4 (.D(fa4_1_s[3]), .EN(1'b1), .CLK(clock_1_out), .R(or_1_out), .Q(a1[3]));
  My7SegmentDecoder my7segmentdecoder_1 (
    .In_1(a1), .in_2(1'b1), .G(my7segmentdecoder_1_g), .F(my7segmentdecoder_1_f), .A(my7segmentdecoder_1_a),
    .B(my7segmentdecoder_1_b), .E(my7segmentdecoder_1_e), .D(my7segmentdecoder_1_d), .C(my7segmentdecoder_1_c));
  My7SegmentDecoder my7segmentdecoder_2 (
    .In_1(a2), .in_2(1'b1), .G(my7segmentdecoder_2_g), .F(my7segmentdecoder_2_f), .A(my7segmentdecoder_2_a),
    .B(my7segmentdecoder_2_b), .E(my7segmentdecoder_2_e), .D(my7segmentdecoder_2_d), .C(my7segmentdecoder_2_c));
  My7SegmentDecoder my7segmentdecoder_3 (
    .In_1(a4), .in_2(1'b1), .G(my7segmentdecoder_3_g), .F(my7segmentdecoder_3_f), .A(my7segmentdecoder_3_a),
    .B(my7segmentdecoder_3_b), .E(my7segmentdecoder_3_e), .D(my7segmentdecoder_3_d), .C(my7segmentdecoder_3_c));
  xnor xnor_5 (xnor_5_out, a2[0], 1'b0);
  xnor xnor_6 (xnor_6_out, a2[1], 1'b1);
  xnor xnor_7 (xnor_7_out, a2[2], 1'b1);
  xnor xnor_8 (xnor_8_out, a2[3], 1'b0);
  and and_2 (b2, xnor_5_out, xnor_6_out, xnor_7_out, xnor_8_out);
  and and_3 (and_3_out, b1, 1'b1);
  FA4 fa4_2 (.A(4'b0001), .B(a2), .S(fa4_2_s));  // open: Cin, Cout
  or or_2 (or_2_out, button_1_out, b2);
  DFlipFlop dflipflop_5 (.D(fa4_2_s[0]), .EN(1'b1), .CLK(and_3_out), .R(or_2_out), .Q(a2[0]));
  DFlipFlop dflipflop_6 (.D(fa4_2_s[1]), .EN(1'b1), .CLK(and_3_out), .R(or_2_out), .Q(a2[1]));
  DFlipFlop dflipflop_7 (.D(fa4_2_s[2]), .EN(1'b1), .CLK(and_3_out), .R(or_2_out), .Q(a2[2]));
  DFlipFlop dflipflop_8 (.D(fa4_2_s[3]), .EN(1'b1), .CLK(and_3_out), .R(or_2_out), .Q(a2[3]));
  _7_Segment_Display u_7_segment_display_1 (
    .g(my7segmentdecoder_3_g), .f(my7segmentdecoder_3_f), .a(my7segmentdecoder_3_a),
    .b(my7segmentdecoder_3_b), .e(my7segmentdecoder_3_e), .d(my7segmentdecoder_3_d), .c(my7segmentdecoder_3_c));  // open: dp
  _7_Segment_Display u_7_segment_display_2 (
    .g(my7segmentdecoder_4_g), .f(my7segmentdecoder_4_f), .a(my7segmentdecoder_4_a),
    .b(my7segmentdecoder_4_b), .e(my7segmentdecoder_4_e), .d(my7segmentdecoder_4_d), .c(my7segmentdecoder_4_c));  // open: dp
  _7_Segment_Display u_7_segment_display_3 (
    .g(my7segmentdecoder_2_g), .f(my7segmentdecoder_2_f), .a(my7segmentdecoder_2_a),
    .b(my7segmentdecoder_2_b), .e(my7segmentdecoder_2_e), .d(my7segmentdecoder_2_d), .c(my7segmentdecoder_2_c));  // open: dp
  xnor xnor_9 (xnor_9_out, a3[0], 1'b0);
  xnor xnor_10 (xnor_10_out, a3[1], 1'b1);
  xnor xnor_11 (xnor_11_out, a3[2], 1'b0);
  xnor xnor_12 (xnor_12_out, a3[3], 1'b1);
  and and_4 (and_4_out, 1'b1, b2);
  _7_Segment_Display u_7_segment_display_4 (
    .g(my7segmentdecoder_1_g), .f(my7segmentdecoder_1_f), .a(my7segmentdecoder_1_a),
    .b(my7segmentdecoder_1_b), .e(my7segmentdecoder_1_e), .d(my7segmentdecoder_1_d), .c(my7segmentdecoder_1_c));  // open: dp
  and and_5 (b3, xnor_9_out, xnor_10_out, xnor_11_out, xnor_12_out);
  or or_3 (or_3_out, button_1_out, b3);
  DFlipFlop dflipflop_9 (.D(fa4_3_s[0]), .EN(1'b1), .CLK(and_4_out), .R(or_3_out), .Q(a3[0]));
  DFlipFlop dflipflop_10 (.D(fa4_3_s[1]), .EN(1'b1), .CLK(and_4_out), .R(or_3_out), .Q(a3[1]));
  DFlipFlop dflipflop_11 (.D(fa4_3_s[2]), .EN(1'b1), .CLK(and_4_out), .R(or_3_out), .Q(a3[2]));
  DFlipFlop dflipflop_12 (.D(fa4_3_s[3]), .EN(1'b1), .CLK(and_4_out), .R(or_3_out), .Q(a3[3]));
  My7SegmentDecoder my7segmentdecoder_4 (
    .In_1(a3), .in_2(1'b1), .G(my7segmentdecoder_4_g), .F(my7segmentdecoder_4_f), .A(my7segmentdecoder_4_a),
    .B(my7segmentdecoder_4_b), .E(my7segmentdecoder_4_e), .D(my7segmentdecoder_4_d), .C(my7segmentdecoder_4_c));
  FA4 fa4_3 (.A(4'b0001), .B(a3), .S(fa4_3_s));  // open: Cin, Cout
  xnor xnor_13 (xnor_13_out, a4[0], 1'b0);
  xnor xnor_14 (xnor_14_out, a4[1], 1'b1);
  xnor xnor_15 (xnor_15_out, a4[2], 1'b1);
  xnor xnor_16 (xnor_16_out, a4[3], 1'b0);
  and and_6 (and_6_out, 1'b1, b3);
  and and_7 (b4, xnor_13_out, xnor_14_out, xnor_15_out, xnor_16_out);
  or or_4 (or_4_out, button_1_out, b4);
  FA4 fa4_4 (.A(4'b0001), .B(a4), .S(fa4_4_s));  // open: Cin, Cout
  DFlipFlop dflipflop_13 (.D(fa4_4_s[0]), .EN(1'b1), .CLK(and_6_out), .R(or_4_out), .Q(a4[0]));
  DFlipFlop dflipflop_14 (.D(fa4_4_s[1]), .EN(1'b1), .CLK(and_6_out), .R(or_4_out), .Q(a4[1]));
  DFlipFlop dflipflop_15 (.D(fa4_4_s[2]), .EN(1'b1), .CLK(and_6_out), .R(or_4_out), .Q(a4[2]));
  DFlipFlop dflipflop_16 (.D(fa4_4_s[3]), .EN(1'b1), .CLK(and_6_out), .R(or_4_out), .Q(a4[3]));
endmodule

module ct (
  input  [7:0] pc_in,
  input  clk,
  input  R,
  input  en,
  output [7:0] pc_out
);

  wire not_1_out;
  wire [7:0] and_1_out, and_9_out, fa8_1_s, or_1_out;

  not not_1 (not_1_out, en);
  and and_1 (and_1_out[0], pc_in[0], en);
  and and_2 (and_1_out[1], pc_in[1], en);
  and and_3 (and_1_out[2], pc_in[2], en);
  and and_4 (and_1_out[3], pc_in[3], en);
  and and_5 (and_1_out[4], pc_in[4], en);
  and and_6 (and_1_out[5], pc_in[5], en);
  and and_7 (and_1_out[6], pc_in[6], en);
  and and_8 (and_1_out[7], pc_in[7], en);
  FA8 fa8_1 (.A(pc_out), .B(8'h1), .S(fa8_1_s));  // open: Cin, Cout
  and and_9 (and_9_out[0], fa8_1_s[0], not_1_out);
  and and_10 (and_9_out[1], fa8_1_s[1], not_1_out);
  and and_11 (and_9_out[2], fa8_1_s[2], not_1_out);
  and and_12 (and_9_out[3], fa8_1_s[3], not_1_out);
  and and_13 (and_9_out[4], fa8_1_s[4], not_1_out);
  and and_14 (and_9_out[5], fa8_1_s[5], not_1_out);
  and and_15 (and_9_out[6], fa8_1_s[6], not_1_out);
  and and_16 (and_9_out[7], fa8_1_s[7], not_1_out);
  assign or_1_out = and_1_out | and_9_out;  // OR_Gate or_1, 8 bits wide
  DFlipFlop dflipflop_1 (.D(or_1_out[0]), .EN(1'b1), .CLK(clk), .R(R), .Q(pc_out[0]));
  DFlipFlop dflipflop_2 (.D(or_1_out[1]), .EN(1'b1), .CLK(clk), .R(R), .Q(pc_out[1]));
  DFlipFlop dflipflop_3 (.D(or_1_out[2]), .EN(1'b1), .CLK(clk), .R(R), .Q(pc_out[2]));
  DFlipFlop dflipflop_4 (.D(or_1_out[3]), .EN(1'b1), .CLK(clk), .R(R), .Q(pc_out[3]));
  DFlipFlop dflipflop_5 (.D(or_1_out[4]), .EN(1'b1), .CLK(clk), .R(R), .Q(pc_out[4]));
  DFlipFlop dflipflop_6 (.D(or_1_out[5]), .EN(1'b1), .CLK(clk), .R(R), .Q(pc_out[5]));
  DFlipFlop dflipflop_7 (.D(or_1_out[6]), .EN(1'b1), .CLK(clk), .R(R), .Q(pc_out[6]));
  DFlipFlop dflipflop_8 (.D(or_1_out[7]), .EN(1'b1), .CLK(clk), .R(R), .Q(pc_out[7]));
endmodule

module FA8 (
  input  [7:0] A,
  input  Cin,
  input  [7:0] B,
  output [7:0] S,
  output Cout
);

  wire fa_1_cout, fa_2_cout, fa_3_cout, fa_4_cout, fa_5_cout, fa_6_cout, fa_7_cout;

  FA fa_1 (.A(A[0]), .Cin(Cin), .B(B[0]), .S(S[0]), .Cout(fa_1_cout));
  FA fa_2 (.A(A[1]), .Cin(fa_1_cout), .B(B[1]), .S(S[1]), .Cout(fa_2_cout));
  FA fa_3 (.A(A[2]), .Cin(fa_2_cout), .B(B[2]), .S(S[2]), .Cout(fa_3_cout));
  FA fa_4 (.A(A[3]), .Cin(fa_3_cout), .B(B[3]), .S(S[3]), .Cout(fa_4_cout));
  FA fa_5 (.A(A[4]), .Cin(fa_4_cout), .B(B[4]), .S(S[4]), .Cout(fa_5_cout));
  FA fa_6 (.A(A[5]), .Cin(fa_5_cout), .B(B[5]), .S(S[5]), .Cout(fa_6_cout));
  FA fa_7 (.A(A[6]), .Cin(fa_6_cout), .B(B[6]), .S(S[6]), .Cout(fa_7_cout));
  FA fa_8 (.A(A[7]), .Cin(fa_7_cout), .B(B[7]), .S(S[7]), .Cout(Cout));
endmodule

module Adder1To10 (
);

  wire and_1_out, button_1_out, clock_1_out, not_1_out, t2, x0, x1, x2, x3, x4, x5, x6, x7, xnor_1_out,
       xnor_2_out, xnor_3_out, xnor_4_out;
  wire [3:0] t1;
  wire [7:0] fa8_1_s;

  Clock clock_1 (.out(clock_1_out));
  not not_1 (not_1_out, t2);
  and and_1 (and_1_out, clock_1_out, not_1_out);
  Button button_1 (.out(button_1_out));
  xnor xnor_1 (xnor_1_out, t1[0], 1'b1);
  xnor xnor_2 (xnor_2_out, t1[1], 1'b1);
  xnor xnor_3 (xnor_3_out, t1[2], 1'b0);
  xnor xnor_4 (xnor_4_out, t1[3], 1'b1);
  and and_2 (t2, xnor_1_out, xnor_2_out, xnor_3_out, xnor_4_out);
  // ct ct_1: pin names not known; wires that end beside it: and_1_out, button_1_out, t1
  // Probe on {4'b0000, t1}
  // Probe on {x7, x6, x5, x4, x3, x2, x1, x0}
  DFlipFlop dflipflop_1 (.D(fa8_1_s[4]), .EN(1'b1), .CLK(and_1_out), .R(button_1_out), .Q(x4));
  DFlipFlop dflipflop_2 (.D(fa8_1_s[5]), .EN(1'b1), .CLK(and_1_out), .R(button_1_out), .Q(x5));
  DFlipFlop dflipflop_3 (.D(fa8_1_s[6]), .EN(1'b1), .CLK(and_1_out), .R(button_1_out), .Q(x6));
  DFlipFlop dflipflop_4 (.D(fa8_1_s[7]), .EN(1'b1), .CLK(and_1_out), .R(button_1_out), .Q(x7));
  FA8 fa8_1 (.A({4'b0000, t1}), .B({x7, x6, x5, x4, x3, x2, x1, x0}), .S(fa8_1_s));  // open: Cin, Cout
  DFlipFlop dflipflop_5 (.D(fa8_1_s[0]), .EN(1'b1), .CLK(and_1_out), .R(button_1_out), .Q(x0));
  DFlipFlop dflipflop_6 (.D(fa8_1_s[1]), .EN(1'b1), .CLK(and_1_out), .R(button_1_out), .Q(x1));
  DFlipFlop dflipflop_7 (.D(fa8_1_s[2]), .EN(1'b1), .CLK(and_1_out), .R(button_1_out), .Q(x2));
  DFlipFlop dflipflop_8 (.D(fa8_1_s[3]), .EN(1'b1), .CLK(and_1_out), .R(button_1_out), .Q(x3));
endmodule

module FA4 (
  input  [3:0] A,
  input  Cin,
  input  [3:0] B,
  output [3:0] S,
  output Cout
);

  wire fa_1_cout, fa_2_cout, fa_3_cout;

  FA fa_1 (.A(A[0]), .Cin(Cin), .B(B[0]), .S(S[0]), .Cout(fa_1_cout));
  FA fa_2 (.A(A[1]), .Cin(fa_1_cout), .B(B[1]), .S(S[1]), .Cout(fa_2_cout));
  FA fa_3 (.A(A[2]), .Cin(fa_2_cout), .B(B[2]), .S(S[2]), .Cout(fa_3_cout));
  FA fa_4 (.A(A[3]), .Cin(fa_3_cout), .B(B[3]), .S(S[3]), .Cout(Cout));
endmodule

module a (
  input  [7:0] wdata,
  input  clk,
  input  R,
  input  [1:0] waddr,
  input  EN,
  input  [1:0] addr1,
  input  [1:0] addr2,
  output [7:0] data1,
  output [7:0] data2
);

  wire and_1_out, and_2_out, and_3_out, and_4_out, and_5_out, and_6_out, and_7_out, and_8_out, and_9_out,
       and_10_out, and_11_out, and_12_out, and_13_out, and_14_out, and_15_out, and_16_out, and_17_out,
       and_18_out, and_19_out, and_20_out, and_21_out, and_22_out, and_23_out, and_24_out, and_25_out,
       and_26_out, and_27_out, and_28_out, and_29_out, and_30_out, and_31_out, and_32_out, and_33_out,
       and_34_out, and_35_out, and_36_out, and_37_out, and_38_out, and_39_out, and_40_out, and_41_out,
       and_42_out, and_43_out, and_44_out, and_45_out, and_46_out, and_47_out, and_48_out, and_49_out,
       and_50_out, and_51_out, and_52_out, and_53_out, and_54_out, and_55_out, and_56_out, and_57_out,
       and_58_out, and_59_out, and_60_out, and_61_out, and_62_out, and_63_out, and_64_out, and_65_out,
       and_66_out, and_67_out, and_68_out, and_69_out, and_70_out, and_71_out, and_72_out, and_73_out,
       and_74_out, and_75_out, and_76_out, and_77_out, and_78_out, and_79_out, and_80_out, and_81_out,
       and_82_out, and_83_out, and_84_out, and_85_out, and_86_out, and_87_out, and_88_out, and_89_out,
       and_90_out, and_91_out, and_92_out, and_93_out, and_94_out, and_95_out, and_96_out, and_97_out,
       and_98_out, and_99_out, and_100_out, and_101_out, and_102_out, and_103_out, and_104_out, and_105_out,
       and_106_out, and_107_out, and_108_out, and_109_out, and_110_out, and_111_out, and_112_out,
       and_113_out, and_114_out, and_115_out, and_116_out, and_117_out, and_118_out, and_119_out,
       and_120_out, and_121_out, and_122_out, and_123_out, and_124_out, and_125_out, and_126_out,
       and_127_out, and_128_out, and_129_out, and_130_out, and_131_out, and_132_out, and_141_out,
       and_142_out, and_143_out, and_144_out, and_145_out, and_146_out, and_147_out, and_148_out,
       and_149_out, and_150_out, and_151_out, and_152_out, and_153_out, and_154_out, and_155_out,
       and_156_out, and_157_out, and_158_out, and_159_out, and_160_out, and_161_out, and_162_out,
       and_163_out, and_164_out, and_165_out, and_166_out, and_167_out, and_168_out, and_169_out,
       and_170_out, and_171_out, and_172_out, and_193_out, and_194_out, and_195_out, and_196_out,
       and_197_out, and_198_out, and_199_out, and_200_out, and_201_out, and_202_out, and_203_out,
       and_204_out, and_205_out, and_206_out, and_207_out, and_208_out, and_209_out, and_210_out,
       and_211_out, and_212_out, and_213_out, and_214_out, and_215_out, and_216_out, and_217_out,
       and_218_out, and_219_out, and_220_out, and_221_out, and_222_out, and_223_out, and_224_out,
       and_261_out, and_262_out, and_263_out, and_264_out, and_265_out, and_266_out, and_267_out,
       and_268_out, and_269_out, and_270_out, and_271_out, and_272_out, and_273_out, and_274_out,
       and_275_out, and_276_out, and_277_out, and_278_out, and_279_out, and_280_out, and_281_out,
       and_282_out, and_283_out, and_284_out, and_285_out, and_286_out, and_287_out, and_288_out,
       and_289_out, and_290_out, and_291_out, and_292_out, and_293_out, and_294_out, and_295_out,
       and_296_out, and_297_out, and_298_out, and_299_out, and_300_out, and_301_out, and_302_out,
       and_303_out, and_304_out, and_305_out, and_306_out, and_307_out, and_308_out, and_309_out,
       and_310_out, and_311_out, and_312_out, and_313_out, and_314_out, and_315_out, and_316_out,
       and_317_out, and_318_out, and_319_out, and_320_out, and_321_out, and_322_out, and_323_out,
       and_324_out, mydecoder2to4_1_out_2, mydecoder2to4_1_out_3, mydecoder2to4_1_out_4,
       mydecoder2to4_1_out_5, mydecoder2to4_2_out_2, mydecoder2to4_3_out_2, mydecoder2to4_3_out_3,
       mydecoder2to4_3_out_4, mydecoder2to4_3_out_5, r1, r3, r4, s1, s2, s3, s4, s5, s6, s7, s8, s9, s10,
       s11, s12, s13, s14, s15, s16, s17, s18, s19, s20, s21, s22, s23, s24, s25, s26, s27, s28, s29, s30,
       s31, s32, t1, t2, t3, t4, t5, t6, t7, t8, t9, t10, t11, t12, t13, t14, t15, t16, t17, t18, t19, t20,
       t21, t22, t23, t24, t25, t26, t27, t28, t29, t30, t31, t32, u1, u2, u3, u4, u5, u6, u7, u8, u9, u10,
       u11, u12, u13, u14, u15, u16, u17, u18, u19, u20, u21, u22, u23, u24, u25, u26, u27, u28, u29, u30,
       u31, u32;
  wire [3:0] or_1_out, or_5_out, or_9_out, or_13_out, or_17_out, or_21_out, or_25_out, or_29_out, or_34_out,
       or_38_out, or_42_out, or_46_out, or_51_out, or_55_out, or_59_out, or_63_out;

  and and_1 (and_1_out, r3, t13);
  and and_2 (and_2_out, r3, t14);
  and and_3 (and_3_out, r3, t15);
  and and_4 (and_4_out, r3, t16);
  and and_5 (and_5_out, r3, t9);
  and and_6 (and_6_out, r3, t10);
  and and_7 (and_7_out, r3, t11);
  and and_8 (and_8_out, r3, t12);
  and and_9 (and_9_out, r3, t5);
  and and_10 (and_10_out, r3, t6);
  and and_11 (and_11_out, r3, t7);
  and and_12 (and_12_out, r3, t8);
  and and_13 (and_13_out, r3, t1);
  and and_14 (and_14_out, r3, t2);
  and and_15 (and_15_out, r3, t3);
  and and_16 (and_16_out, r3, t4);
  and and_17 (and_17_out, r3, t29);
  and and_18 (and_18_out, r3, t30);
  and and_19 (and_19_out, r3, t31);
  and and_20 (and_20_out, r3, t32);
  and and_21 (and_21_out, r3, t25);
  and and_22 (and_22_out, r3, t26);
  and and_23 (and_23_out, r3, t27);
  and and_24 (and_24_out, r3, t28);
  and and_25 (and_25_out, r3, t21);
  and and_26 (and_26_out, r3, t22);
  and and_27 (and_27_out, r3, t23);
  and and_28 (and_28_out, r3, t24);
  and and_29 (and_29_out, r3, t17);
  and and_30 (and_30_out, r3, t18);
  and and_31 (and_31_out, r3, t19);
  and and_32 (and_32_out, r3, t20);
  and and_33 (and_33_out, r4, t13);
  and and_34 (and_34_out, r4, t14);
  and and_35 (and_35_out, r4, t15);
  and and_36 (and_36_out, r4, t16);
  and and_37 (and_37_out, r4, t9);
  and and_38 (and_38_out, r4, t10);
  and and_39 (and_39_out, r4, t11);
  and and_40 (and_40_out, r4, t12);
  and and_41 (and_41_out, r4, t5);
  and and_42 (and_42_out, r4, t6);
  and and_43 (and_43_out, r4, t7);
  and and_44 (and_44_out, r4, t8);
  and and_45 (and_45_out, r4, t1);
  and and_46 (and_46_out, r4, t2);
  and and_47 (and_47_out, r4, t3);
  and and_48 (and_48_out, r4, t4);
  and and_49 (and_49_out, r4, t29);
  and and_50 (and_50_out, r4, t30);
  and and_51 (and_51_out, r4, t31);
  and and_52 (and_52_out, r4, t32);
  and and_53 (and_53_out, r4, t25);
  and and_54 (and_54_out, r4, t26);
  and and_55 (and_55_out, r4, t27);
  and and_56 (and_56_out, r4, t28);
  and and_57 (and_57_out, r4, t21);
  and and_58 (and_58_out, r4, t22);
  and and_59 (and_59_out, r4, t23);
  and and_60 (and_60_out, r4, t24);
  and and_61 (and_61_out, r4, t17);
  and and_62 (and_62_out, r4, t18);
  and and_63 (and_63_out, r4, t19);
  and and_64 (and_64_out, r4, t20);
  or or_1 (or_1_out[0], and_1_out, and_2_out, and_3_out, and_4_out);
  or or_2 (or_1_out[1], and_5_out, and_6_out, and_7_out, and_8_out);
  or or_3 (or_1_out[2], and_9_out, and_10_out, and_11_out, and_12_out);
  or or_4 (or_1_out[3], and_13_out, and_14_out, and_15_out, and_16_out);
  or or_5 (or_5_out[0], and_17_out, and_18_out, and_19_out, and_20_out);
  or or_6 (or_5_out[1], and_21_out, and_22_out, and_23_out, and_24_out);
  or or_7 (or_5_out[2], and_25_out, and_26_out, and_27_out, and_28_out);
  or or_8 (or_5_out[3], and_29_out, and_30_out, and_31_out, and_32_out);
  or or_9 (or_9_out[0], and_33_out, and_34_out, and_35_out, and_36_out);
  or or_10 (or_9_out[1], and_37_out, and_38_out, and_39_out, and_40_out);
  or or_11 (or_9_out[2], and_41_out, and_42_out, and_43_out, and_44_out);
  or or_12 (or_9_out[3], and_45_out, and_46_out, and_47_out, and_48_out);
  or or_13 (or_13_out[0], and_49_out, and_50_out, and_51_out, and_52_out);
  or or_14 (or_13_out[1], and_53_out, and_54_out, and_55_out, and_56_out);
  or or_15 (or_13_out[2], and_57_out, and_58_out, and_59_out, and_60_out);
  or or_16 (or_13_out[3], and_61_out, and_62_out, and_63_out, and_64_out);
  MyDecoder2To4 mydecoder2to4_1 (
    .in_1(waddr), .out_2(mydecoder2to4_1_out_2), .out_3(mydecoder2to4_1_out_3),
    .out_4(mydecoder2to4_1_out_4), .out_5(mydecoder2to4_1_out_5));
  MyDecoder2To4 mydecoder2to4_2 (.in_1(addr1), .out_2(mydecoder2to4_2_out_2), .out_3(r1), .out_4(r3), .out_5(r4));
  and and_65 (and_65_out, mydecoder2to4_2_out_2, t13);
  and and_66 (and_66_out, mydecoder2to4_2_out_2, t14);
  and and_67 (and_67_out, mydecoder2to4_2_out_2, t15);
  and and_68 (and_68_out, mydecoder2to4_2_out_2, t16);
  and and_69 (and_69_out, mydecoder2to4_2_out_2, t9);
  and and_70 (and_70_out, mydecoder2to4_2_out_2, t10);
  and and_71 (and_71_out, mydecoder2to4_2_out_2, t11);
  and and_72 (and_72_out, mydecoder2to4_2_out_2, t12);
  and and_73 (and_73_out, mydecoder2to4_2_out_2, t5);
  and and_74 (and_74_out, mydecoder2to4_2_out_2, t6);
  and and_75 (and_75_out, mydecoder2to4_2_out_2, t7);
  and and_76 (and_76_out, mydecoder2to4_2_out_2, t8);
  and and_77 (and_77_out, mydecoder2to4_2_out_2, t1);
  and and_78 (and_78_out, mydecoder2to4_2_out_2, t2);
  and and_79 (and_79_out, mydecoder2to4_2_out_2, t3);
  and and_80 (and_80_out, mydecoder2to4_2_out_2, t4);
  and and_81 (and_81_out, mydecoder2to4_2_out_2, t29);
  and and_82 (and_82_out, mydecoder2to4_2_out_2, t30);
  and and_83 (and_83_out, mydecoder2to4_2_out_2, t31);
  and and_84 (and_84_out, mydecoder2to4_2_out_2, t32);
  and and_85 (and_85_out, mydecoder2to4_2_out_2, t25);
  and and_86 (and_86_out, mydecoder2to4_2_out_2, t26);
  and and_87 (and_87_out, mydecoder2to4_2_out_2, t27);
  and and_88 (and_88_out, mydecoder2to4_2_out_2, t28);
  and and_89 (and_89_out, mydecoder2to4_2_out_2, t21);
  and and_90 (and_90_out, mydecoder2to4_2_out_2, t22);
  and and_91 (and_91_out, mydecoder2to4_2_out_2, t23);
  and and_92 (and_92_out, mydecoder2to4_2_out_2, t24);
  and and_93 (and_93_out, mydecoder2to4_2_out_2, t17);
  and and_94 (and_94_out, mydecoder2to4_2_out_2, t18);
  and and_95 (and_95_out, mydecoder2to4_2_out_2, t19);
  and and_96 (and_96_out, mydecoder2to4_2_out_2, t20);
  and and_97 (and_97_out, r1, t13);
  and and_98 (and_98_out, r1, t14);
  and and_99 (and_99_out, r1, t15);
  and and_100 (and_100_out, r1, t16);
  and and_101 (and_101_out, r1, t9);
  and and_102 (and_102_out, r1, t10);
  and and_103 (and_103_out, r1, t11);
  buf and_104 (and_104_out, t12);  // AND_Gate
  and and_105 (and_105_out, r1, t5);
  and and_106 (and_106_out, r1, t6);
  and and_107 (and_107_out, r1, t7);
  and and_108 (and_108_out, r1, t8);
  and and_109 (and_109_out, r1, t1);
  and and_110 (and_110_out, r1, t2);
  and and_111 (and_111_out, r1, t3);
  and and_112 (and_112_out, r1, t4);
  and and_113 (and_113_out, r1, t29);
  and and_114 (and_114_out, r1, t30);
  and and_115 (and_115_out, r1, t31);
  and and_116 (and_116_out, r1, t32);
  and and_117 (and_117_out, r1, t25);
  and and_118 (and_118_out, r1, t26);
  and and_119 (and_119_out, r1, t27);
  and and_120 (and_120_out, r1, t28);
  and and_121 (and_121_out, r1, t21);
  and and_122 (and_122_out, r1, t22);
  and and_123 (and_123_out, r1, t23);
  and and_124 (and_124_out, r1, t24);
  and and_125 (and_125_out, r1, t17);
  and and_126 (and_126_out, r1, t18);
  and and_127 (and_127_out, r1, t19);
  and and_128 (and_128_out, r1, t20);
  or or_17 (or_17_out[0], and_65_out, and_66_out, and_67_out, and_68_out);
  or or_18 (or_17_out[1], and_69_out, and_70_out, and_71_out, and_72_out);
  or or_19 (or_17_out[2], and_73_out, and_74_out, and_75_out, and_76_out);
  or or_20 (or_17_out[3], and_77_out, and_78_out, and_79_out, and_80_out);
  or or_21 (or_21_out[0], and_81_out, and_82_out, and_83_out, and_84_out);
  or or_22 (or_21_out[1], and_85_out, and_86_out, and_87_out, and_88_out);
  or or_23 (or_21_out[2], and_89_out, and_90_out, and_91_out, and_92_out);
  or or_24 (or_21_out[3], and_93_out, and_94_out, and_95_out, and_96_out);
  or or_25 (or_25_out[0], and_97_out, and_98_out, and_99_out, and_100_out);
  or or_26 (or_25_out[1], and_101_out, and_102_out, and_103_out, and_104_out);
  or or_27 (or_25_out[2], and_105_out, and_106_out, and_107_out, and_108_out);
  or or_28 (or_25_out[3], and_109_out, and_110_out, and_111_out, and_112_out);
  or or_29 (or_29_out[0], and_113_out, and_114_out, and_115_out, and_116_out);
  or or_30 (or_29_out[1], and_117_out, and_118_out, and_119_out, and_120_out);
  or or_31 (or_29_out[2], and_121_out, and_122_out, and_123_out, and_124_out);
  or or_32 (or_29_out[3], and_125_out, and_126_out, and_127_out, and_128_out);
  and and_129 (and_129_out, EN, mydecoder2to4_1_out_2);
  and and_130 (and_130_out, EN, mydecoder2to4_1_out_3);
  and and_131 (and_131_out, EN, mydecoder2to4_1_out_4);
  and and_132 (and_132_out, EN, mydecoder2to4_1_out_5);
  DFlipFlop dflipflop_1 (.D(wdata[7]), .EN(and_129_out), .CLK(clk), .R(R), .Q(s1));
  DFlipFlop dflipflop_2 (.D(wdata[7]), .EN(and_130_out), .CLK(clk), .R(R), .Q(s9));
  DFlipFlop dflipflop_3 (.D(wdata[7]), .EN(and_131_out), .CLK(clk), .R(R), .Q(s17));
  DFlipFlop dflipflop_4 (.D(wdata[7]), .EN(and_132_out), .CLK(clk), .R(R), .Q(s25));
  and and_133 (t19, r1, s9);
  and and_134 (t18, r3, s17);
  and and_135 (t17, r4, s25);
  assign data1 = {or_5_out, or_1_out} | {or_21_out, or_17_out} | {or_13_out, or_9_out} | {or_29_out, or_25_out};  // OR_Gate or_33, 8 bits wide
  and and_136 (t20, mydecoder2to4_2_out_2, s1);
  DFlipFlop dflipflop_5 (.D(wdata[6]), .EN(and_129_out), .CLK(clk), .R(R), .Q(s2));
  DFlipFlop dflipflop_6 (.D(wdata[6]), .EN(and_130_out), .CLK(clk), .R(R), .Q(s10));
  DFlipFlop dflipflop_7 (.D(wdata[6]), .EN(and_131_out), .CLK(clk), .R(R), .Q(s18));
  DFlipFlop dflipflop_8 (.D(wdata[6]), .EN(and_132_out), .CLK(clk), .R(R), .Q(s26));
  and and_137 (t24, mydecoder2to4_2_out_2, s2);
  and and_138 (t23, r1, s10);
  and and_139 (t22, r3, s18);
  and and_140 (t21, r4, s26);
  MyDecoder2To4 mydecoder2to4_3 (
    .in_1(addr2), .out_2(mydecoder2to4_3_out_2), .out_3(mydecoder2to4_3_out_3),
    .out_4(mydecoder2to4_3_out_4), .out_5(mydecoder2to4_3_out_5));
  and and_141 (and_141_out, mydecoder2to4_3_out_4, u13);
  and and_142 (and_142_out, mydecoder2to4_3_out_4, u14);
  and and_143 (and_143_out, mydecoder2to4_3_out_4, u15);
  and and_144 (and_144_out, mydecoder2to4_3_out_4, u16);
  and and_145 (and_145_out, mydecoder2to4_3_out_4, u9);
  and and_146 (and_146_out, mydecoder2to4_3_out_4, u10);
  and and_147 (and_147_out, mydecoder2to4_3_out_4, u11);
  and and_148 (and_148_out, mydecoder2to4_3_out_4, u12);
  and and_149 (and_149_out, mydecoder2to4_3_out_4, u5);
  and and_150 (and_150_out, mydecoder2to4_3_out_4, u6);
  and and_151 (and_151_out, mydecoder2to4_3_out_4, u7);
  and and_152 (and_152_out, mydecoder2to4_3_out_4, u8);
  and and_153 (and_153_out, mydecoder2to4_3_out_4, u1);
  and and_154 (and_154_out, mydecoder2to4_3_out_4, u2);
  and and_155 (and_155_out, mydecoder2to4_3_out_4, u3);
  and and_156 (and_156_out, mydecoder2to4_3_out_4, u4);
  and and_157 (and_157_out, mydecoder2to4_3_out_4, u32);
  and and_158 (and_158_out, mydecoder2to4_3_out_4, u31);
  and and_159 (and_159_out, mydecoder2to4_3_out_4, u30);
  and and_160 (and_160_out, mydecoder2to4_3_out_4, u29);
  and and_161 (and_161_out, mydecoder2to4_3_out_4, u28);
  and and_162 (and_162_out, mydecoder2to4_3_out_4, u27);
  and and_163 (and_163_out, mydecoder2to4_3_out_4, u26);
  and and_164 (and_164_out, mydecoder2to4_3_out_4, u25);
  and and_165 (and_165_out, mydecoder2to4_3_out_4, u24);
  and and_166 (and_166_out, mydecoder2to4_3_out_4, u23);
  and and_167 (and_167_out, mydecoder2to4_3_out_4, u22);
  and and_168 (and_168_out, mydecoder2to4_3_out_4, u21);
  and and_169 (and_169_out, mydecoder2to4_3_out_4, t20);
  and and_170 (and_170_out, mydecoder2to4_3_out_4, u19);
  and and_171 (and_171_out, mydecoder2to4_3_out_4, u18);
  and and_172 (and_172_out, mydecoder2to4_3_out_4, u17);
  or or_34 (or_34_out[0], and_141_out, and_142_out, and_143_out, and_144_out);
  or or_35 (or_34_out[1], and_145_out, and_146_out, and_147_out, and_148_out);
  or or_36 (or_34_out[2], and_149_out, and_150_out, and_151_out, and_152_out);
  or or_37 (or_34_out[3], and_153_out, and_154_out, and_155_out, and_156_out);
  or or_38 (or_38_out[0], and_157_out, and_158_out, and_159_out, and_160_out);
  or or_39 (or_38_out[1], and_161_out, and_162_out, and_163_out, and_164_out);
  or or_40 (or_38_out[2], and_165_out, and_166_out, and_167_out, and_168_out);
  or or_41 (or_38_out[3], and_169_out, and_170_out, and_171_out, and_172_out);
  DFlipFlop dflipflop_9 (.D(wdata[5]), .EN(and_129_out), .CLK(clk), .R(R), .Q(s3));
  DFlipFlop dflipflop_10 (.D(wdata[5]), .EN(and_130_out), .CLK(clk), .R(R), .Q(s11));
  DFlipFlop dflipflop_11 (.D(wdata[5]), .EN(and_131_out), .CLK(clk), .R(R), .Q(s19));
  and and_173 (t25, r4, s27);
  DFlipFlop dflipflop_12 (.D(wdata[5]), .EN(and_132_out), .CLK(clk), .R(R), .Q(s27));
  and and_174 (u1, mydecoder2to4_3_out_2, s1);
  and and_175 (u2, mydecoder2to4_3_out_3, s9);
  and and_176 (u3, mydecoder2to4_3_out_4, s17);
  and and_177 (u4, mydecoder2to4_3_out_5, s25);
  and and_178 (t28, mydecoder2to4_2_out_2, s3);
  and and_179 (t27, r1, s11);
  and and_180 (t26, r3, s19);
  DFlipFlop dflipflop_13 (.D(wdata[4]), .EN(and_129_out), .CLK(clk), .R(R), .Q(s4));
  DFlipFlop dflipflop_14 (.D(wdata[4]), .EN(and_130_out), .CLK(clk), .R(R), .Q(s12));
  DFlipFlop dflipflop_15 (.D(wdata[4]), .EN(and_131_out), .CLK(clk), .R(R), .Q(s20));
  DFlipFlop dflipflop_16 (.D(wdata[4]), .EN(and_132_out), .CLK(clk), .R(R), .Q(s28));
  and and_181 (u5, mydecoder2to4_3_out_2, s2);
  and and_182 (u6, mydecoder2to4_3_out_3, s10);
  and and_183 (u7, mydecoder2to4_3_out_4, s18);
  and and_184 (u8, mydecoder2to4_3_out_5, s26);
  and and_185 (t32, mydecoder2to4_2_out_2, s4);
  and and_186 (t31, r1, s12);
  and and_187 (t30, r3, s20);
  and and_188 (t29, r4, s28);
  and and_189 (u9, mydecoder2to4_3_out_2, s3);
  and and_190 (u10, mydecoder2to4_3_out_3, s11);
  and and_191 (u11, mydecoder2to4_3_out_4, s19);
  and and_192 (u12, mydecoder2to4_3_out_5, s27);
  and and_193 (and_193_out, mydecoder2to4_3_out_5, u13);
  and and_194 (and_194_out, mydecoder2to4_3_out_5, u14);
  and and_195 (and_195_out, mydecoder2to4_3_out_5, u15);
  and and_196 (and_196_out, mydecoder2to4_3_out_5, u16);
  and and_197 (and_197_out, mydecoder2to4_3_out_5, u9);
  and and_198 (and_198_out, mydecoder2to4_3_out_5, u10);
  and and_199 (and_199_out, mydecoder2to4_3_out_5, u11);
  and and_200 (and_200_out, mydecoder2to4_3_out_5, u12);
  and and_201 (and_201_out, mydecoder2to4_3_out_5, u5);
  and and_202 (and_202_out, mydecoder2to4_3_out_5, u6);
  and and_203 (and_203_out, mydecoder2to4_3_out_5, u7);
  and and_204 (and_204_out, mydecoder2to4_3_out_5, u8);
  and and_205 (and_205_out, mydecoder2to4_3_out_5, u1);
  and and_206 (and_206_out, mydecoder2to4_3_out_5, u2);
  and and_207 (and_207_out, mydecoder2to4_3_out_5, u3);
  and and_208 (and_208_out, mydecoder2to4_3_out_5, u4);
  and and_209 (and_209_out, mydecoder2to4_3_out_5, u32);
  and and_210 (and_210_out, mydecoder2to4_3_out_5, u31);
  and and_211 (and_211_out, mydecoder2to4_3_out_5, u30);
  and and_212 (and_212_out, mydecoder2to4_3_out_5, u29);
  and and_213 (and_213_out, mydecoder2to4_3_out_5, u28);
  and and_214 (and_214_out, mydecoder2to4_3_out_5, u27);
  and and_215 (and_215_out, mydecoder2to4_3_out_5, u26);
  and and_216 (and_216_out, mydecoder2to4_3_out_5, u25);
  and and_217 (and_217_out, mydecoder2to4_3_out_5, u24);
  and and_218 (and_218_out, mydecoder2to4_3_out_5, u23);
  and and_219 (and_219_out, mydecoder2to4_3_out_5, u22);
  and and_220 (and_220_out, mydecoder2to4_3_out_5, u21);
  and and_221 (and_221_out, mydecoder2to4_3_out_5, t20);
  and and_222 (and_222_out, mydecoder2to4_3_out_5, u19);
  and and_223 (and_223_out, mydecoder2to4_3_out_5, u18);
  and and_224 (and_224_out, mydecoder2to4_3_out_5, u17);
  DFlipFlop dflipflop_17 (.D(wdata[3]), .EN(and_129_out), .CLK(clk), .R(R), .Q(s5));
  DFlipFlop dflipflop_18 (.D(wdata[3]), .EN(and_130_out), .CLK(clk), .R(R), .Q(s13));
  DFlipFlop dflipflop_19 (.D(wdata[3]), .EN(and_131_out), .CLK(clk), .R(R), .Q(s21));
  DFlipFlop dflipflop_20 (.D(wdata[3]), .EN(and_132_out), .CLK(clk), .R(R), .Q(s29));
  or or_42 (or_42_out[0], and_193_out, and_194_out, and_195_out, and_196_out);
  or or_43 (or_42_out[1], and_197_out, and_198_out, and_199_out, and_200_out);
  or or_44 (or_42_out[2], and_201_out, and_202_out, and_203_out, and_204_out);
  or or_45 (or_42_out[3], and_205_out, and_206_out, and_207_out, and_208_out);
  or or_46 (or_46_out[0], and_209_out, and_210_out, and_211_out, and_212_out);
  or or_47 (or_46_out[1], and_213_out, and_214_out, and_215_out, and_216_out);
  or or_48 (or_46_out[2], and_217_out, and_218_out, and_219_out, and_220_out);
  or or_49 (or_46_out[3], and_221_out, and_222_out, and_223_out, and_224_out);
  and and_225 (t4, mydecoder2to4_2_out_2, s5);
  and and_226 (t3, r1, s13);
  and and_227 (t2, r3, s21);
  and and_228 (t1, r4, s29);
  and and_229 (u13, mydecoder2to4_3_out_2, s4);
  and and_230 (u14, mydecoder2to4_3_out_3, s12);
  and and_231 (u15, mydecoder2to4_3_out_4, s20);
  and and_232 (u16, mydecoder2to4_3_out_5, s28);
  and and_233 (u17, mydecoder2to4_3_out_2, s5);
  and and_234 (u18, mydecoder2to4_3_out_3, s13);
  and and_235 (u19, mydecoder2to4_3_out_4, s21);
  and and_236 (u20, mydecoder2to4_3_out_5, s29);
  DFlipFlop dflipflop_21 (.D(wdata[2]), .EN(and_129_out), .CLK(clk), .R(R), .Q(s6));
  DFlipFlop dflipflop_22 (.D(wdata[2]), .EN(and_130_out), .CLK(clk), .R(R), .Q(s14));
  and and_237 (t6, r3, s22);
  DFlipFlop dflipflop_23 (.D(wdata[2]), .EN(and_131_out), .CLK(clk), .R(R), .Q(s22));
  and and_238 (t5, r4, s30);
  DFlipFlop dflipflop_24 (.D(wdata[2]), .EN(and_132_out), .CLK(clk), .R(R), .Q(s30));
  and and_239 (t8, mydecoder2to4_2_out_2, s6);
  and and_240 (t7, r1, s14);
  and and_241 (u21, mydecoder2to4_3_out_2, s6);
  and and_242 (u22, mydecoder2to4_3_out_3, s14);
  and and_243 (u23, mydecoder2to4_3_out_4, s22);
  and and_244 (u24, mydecoder2to4_3_out_5, s30);
  assign data2 = {or_59_out, or_63_out} | {or_51_out, or_55_out} | {or_34_out, or_38_out} | {or_42_out, or_46_out};  // OR_Gate or_50, 8 bits wide
  DFlipFlop dflipflop_25 (.D(wdata[1]), .EN(and_129_out), .CLK(clk), .R(R), .Q(s7));
  DFlipFlop dflipflop_26 (.D(wdata[1]), .EN(and_130_out), .CLK(clk), .R(R), .Q(s15));
  DFlipFlop dflipflop_27 (.D(wdata[1]), .EN(and_131_out), .CLK(clk), .R(R), .Q(s23));
  DFlipFlop dflipflop_28 (.D(wdata[1]), .EN(and_132_out), .CLK(clk), .R(R), .Q(s31));
  and and_245 (t12, mydecoder2to4_2_out_2, s7);
  and and_246 (t11, r1, s15);
  and and_247 (t10, r3, s23);
  and and_248 (t9, r4, s31);
  and and_249 (u25, mydecoder2to4_3_out_2, s7);
  and and_250 (u26, mydecoder2to4_3_out_3, s15);
  and and_251 (u27, mydecoder2to4_3_out_4, s23);
  and and_252 (u28, mydecoder2to4_3_out_5, s31);
  DFlipFlop dflipflop_29 (.D(wdata[0]), .EN(and_129_out), .CLK(clk), .R(R), .Q(s8));
  DFlipFlop dflipflop_30 (.D(wdata[0]), .EN(and_130_out), .CLK(clk), .R(R), .Q(s16));
  DFlipFlop dflipflop_31 (.D(wdata[0]), .EN(and_131_out), .CLK(clk), .R(R), .Q(s24));
  DFlipFlop dflipflop_32 (.D(wdata[0]), .EN(and_132_out), .CLK(clk), .R(R), .Q(s32));
  and and_253 (u29, mydecoder2to4_3_out_2, s8);
  and and_254 (u30, mydecoder2to4_3_out_3, s16);
  and and_255 (u31, mydecoder2to4_3_out_4, s24);
  and and_256 (u32, mydecoder2to4_3_out_5, s32);
  and and_257 (t16, mydecoder2to4_2_out_2, s8);
  and and_258 (t15, r1, s16);
  and and_259 (t14, r3, s24);
  and and_260 (t13, r4, s32);
  and and_261 (and_261_out, mydecoder2to4_3_out_3, u13);
  and and_262 (and_262_out, mydecoder2to4_3_out_3, u14);
  and and_263 (and_263_out, mydecoder2to4_3_out_3, u15);
  and and_264 (and_264_out, mydecoder2to4_3_out_3, u16);
  and and_265 (and_265_out, mydecoder2to4_3_out_3, u9);
  and and_266 (and_266_out, mydecoder2to4_3_out_3, u10);
  and and_267 (and_267_out, mydecoder2to4_3_out_3, u11);
  and and_268 (and_268_out, mydecoder2to4_3_out_3, u12);
  and and_269 (and_269_out, mydecoder2to4_3_out_3, u5);
  and and_270 (and_270_out, mydecoder2to4_3_out_3, u6);
  and and_271 (and_271_out, mydecoder2to4_3_out_3, u7);
  and and_272 (and_272_out, mydecoder2to4_3_out_3, u8);
  and and_273 (and_273_out, mydecoder2to4_3_out_3, u1);
  and and_274 (and_274_out, mydecoder2to4_3_out_3, u2);
  and and_275 (and_275_out, mydecoder2to4_3_out_3, u3);
  and and_276 (and_276_out, mydecoder2to4_3_out_3, u4);
  and and_277 (and_277_out, mydecoder2to4_3_out_3, u32);
  and and_278 (and_278_out, mydecoder2to4_3_out_3, u31);
  and and_279 (and_279_out, mydecoder2to4_3_out_3, u30);
  and and_280 (and_280_out, mydecoder2to4_3_out_3, u29);
  and and_281 (and_281_out, mydecoder2to4_3_out_3, u28);
  and and_282 (and_282_out, mydecoder2to4_3_out_3, u27);
  and and_283 (and_283_out, mydecoder2to4_3_out_3, u26);
  and and_284 (and_284_out, mydecoder2to4_3_out_3, u25);
  and and_285 (and_285_out, mydecoder2to4_3_out_3, u24);
  and and_286 (and_286_out, mydecoder2to4_3_out_3, u23);
  and and_287 (and_287_out, mydecoder2to4_3_out_3, u22);
  and and_288 (and_288_out, mydecoder2to4_3_out_3, u21);
  and and_289 (and_289_out, mydecoder2to4_3_out_3, t20);
  and and_290 (and_290_out, mydecoder2to4_3_out_3, u19);
  and and_291 (and_291_out, mydecoder2to4_3_out_3, u18);
  and and_292 (and_292_out, mydecoder2to4_3_out_3, u17);
  or or_51 (or_51_out[0], and_261_out, and_262_out, and_263_out, and_264_out);
  or or_52 (or_51_out[1], and_265_out, and_266_out, and_267_out, and_268_out);
  or or_53 (or_51_out[2], and_269_out, and_270_out, and_271_out, and_272_out);
  or or_54 (or_51_out[3], and_273_out, and_274_out, and_275_out, and_276_out);
  or or_55 (or_55_out[0], and_277_out, and_278_out, and_279_out, and_280_out);
  or or_56 (or_55_out[1], and_281_out, and_282_out, and_283_out, and_284_out);
  or or_57 (or_55_out[2], and_285_out, and_286_out, and_287_out, and_288_out);
  or or_58 (or_55_out[3], and_289_out, and_290_out, and_291_out, and_292_out);
  // Probe on {s1, s2, s3, s4, s5, s6, s7, s8}
  and and_293 (and_293_out, mydecoder2to4_3_out_2, u13);
  and and_294 (and_294_out, mydecoder2to4_3_out_2, u14);
  and and_295 (and_295_out, mydecoder2to4_3_out_2, u15);
  and and_296 (and_296_out, mydecoder2to4_3_out_2, u16);
  and and_297 (and_297_out, mydecoder2to4_3_out_2, u9);
  and and_298 (and_298_out, mydecoder2to4_3_out_2, u10);
  and and_299 (and_299_out, mydecoder2to4_3_out_2, u11);
  and and_300 (and_300_out, mydecoder2to4_3_out_2, u12);
  and and_301 (and_301_out, mydecoder2to4_3_out_2, u8);
  and and_302 (and_302_out, mydecoder2to4_3_out_2, u7);
  and and_303 (and_303_out, mydecoder2to4_3_out_2, u6);
  and and_304 (and_304_out, mydecoder2to4_3_out_2, u5);
  and and_305 (and_305_out, mydecoder2to4_3_out_2, t4);
  and and_306 (and_306_out, mydecoder2to4_3_out_2, u3);
  and and_307 (and_307_out, mydecoder2to4_3_out_2, u2);
  and and_308 (and_308_out, mydecoder2to4_3_out_2, u1);
  and and_309 (and_309_out, mydecoder2to4_3_out_2, u32);
  and and_310 (and_310_out, mydecoder2to4_3_out_2, u31);
  and and_311 (and_311_out, mydecoder2to4_3_out_2, u30);
  and and_312 (and_312_out, mydecoder2to4_3_out_2, u29);
  and and_313 (and_313_out, mydecoder2to4_3_out_2, u28);
  and and_314 (and_314_out, mydecoder2to4_3_out_2, u27);
  and and_315 (and_315_out, mydecoder2to4_3_out_2, u26);
  and and_316 (and_316_out, mydecoder2to4_3_out_2, u25);
  and and_317 (and_317_out, mydecoder2to4_3_out_2, u24);
  and and_318 (and_318_out, mydecoder2to4_3_out_2, u23);
  and and_319 (and_319_out, mydecoder2to4_3_out_2, u22);
  and and_320 (and_320_out, mydecoder2to4_3_out_2, u21);
  and and_321 (and_321_out, mydecoder2to4_3_out_2, t20);
  and and_322 (and_322_out, mydecoder2to4_3_out_2, u19);
  and and_323 (and_323_out, mydecoder2to4_3_out_2, u18);
  and and_324 (and_324_out, mydecoder2to4_3_out_2, u17);
  // Probe on {s9, s10, s11, s12, s13, s14, s15, s16}
  or or_59 (or_59_out[0], and_293_out, and_294_out, and_295_out, and_296_out);
  or or_60 (or_59_out[1], and_297_out, and_298_out, and_299_out, and_300_out);
  or or_61 (or_59_out[2], and_301_out, and_302_out, and_303_out, and_304_out);
  or or_62 (or_59_out[3], and_305_out, and_306_out, and_307_out, and_308_out);
  or or_63 (or_63_out[0], and_309_out, and_310_out, and_311_out, and_312_out);
  or or_64 (or_63_out[1], and_313_out, and_314_out, and_315_out, and_316_out);
  or or_65 (or_63_out[2], and_317_out, and_318_out, and_319_out, and_320_out);
  or or_66 (or_63_out[3], and_321_out, and_322_out, and_323_out, and_324_out);
  // Probe on {s17, s18, s19, s20, s21, s22, s23, s24}
  // Probe on {s25, s26, s27, s28, s29, s30, s31, s32}
endmodule

module b (
  input  [7:0] ct,
  output LSB,
  output out_3,
  output out_4,
  output out_5,
  output out_6,
  output out_7,
  output out_8,
  output MSB
);

  wire and_1_out, and_2_out, and_3_out, and_4_out, and_5_out, and_6_out, and_7_out, and_8_out, and_9_out,
       and_10_out, and_11_out, and_12_out, and_13_out, and_14_out, and_15_out, and_16_out, and_17_out,
       and_18_out, and_19_out, and_20_out, and_21_out, and_22_out, and_23_out, and_24_out, and_25_out,
       and_26_out, and_27_out, and_28_out, and_29_out, and_30_out, and_31_out, and_32_out, and_33_out,
       and_34_out, and_35_out, and_36_out, and_37_out, and_38_out, and_39_out, and_40_out, and_41_out,
       and_42_out, and_43_out, and_44_out, and_45_out, and_46_out, and_47_out, and_48_out, and_49_out,
       and_50_out, and_51_out, and_52_out, and_53_out, and_54_out, and_55_out, and_56_out, and_57_out,
       and_58_out, and_59_out, and_60_out, and_61_out, and_62_out, and_63_out, and_64_out, and_65_out,
       and_66_out, and_67_out, and_68_out, and_69_out, and_70_out, and_71_out, and_72_out, and_73_out,
       and_74_out, and_75_out, and_76_out, and_77_out, and_78_out, and_79_out, and_80_out, and_81_out,
       and_82_out, and_83_out, and_84_out, and_85_out, and_86_out, and_87_out, and_88_out, and_89_out,
       and_90_out, and_91_out, and_92_out, and_93_out, and_94_out, and_95_out, and_96_out, and_97_out,
       and_98_out, and_99_out, and_100_out, and_101_out, and_102_out, and_103_out, and_104_out,
       mydecoder4to16_1_out_3, mydecoder4to16_1_out_4, mydecoder4to16_1_out_5, mydecoder4to16_1_out_6,
       mydecoder4to16_1_out_7, mydecoder4to16_1_out_8, mydecoder4to16_1_out_9, mydecoder4to16_1_out_10,
       mydecoder4to16_1_out_11, mydecoder4to16_1_out_12, mydecoder4to16_1_out_13, mydecoder4to16_1_out_14,
       mydecoder4to16_1_out_15, or_1_out, or_2_out, or_3_out, or_4_out, or_5_out, or_6_out, or_7_out,
       or_8_out, or_9_out, or_10_out, or_11_out, or_12_out, or_13_out, or_14_out, or_15_out, or_16_out,
       or_17_out, or_18_out, or_19_out, or_20_out, or_21_out, or_22_out, or_23_out, or_24_out, or_26_out,
       or_27_out, or_28_out, or_29_out, or_30_out, or_31_out, or_32_out, or_33_out;

  and and_1 (and_1_out, mydecoder4to16_1_out_7, 1'b0);
  and and_2 (and_2_out, mydecoder4to16_1_out_7, 1'b0);
  and and_3 (and_3_out, mydecoder4to16_1_out_8, 1'b0);
  and and_4 (and_4_out, mydecoder4to16_1_out_9, 1'b0);
  and and_5 (and_5_out, mydecoder4to16_1_out_10, 1'b1);
  and and_6 (and_6_out, mydecoder4to16_1_out_11, 1'b1);
  or or_1 (or_1_out, and_1_out, and_3_out, and_4_out, and_5_out, and_6_out);
  and and_7 (and_7_out, mydecoder4to16_1_out_7, 1'b0);
  and and_8 (and_8_out, mydecoder4to16_1_out_8, 1'b1);
  and and_9 (and_9_out, mydecoder4to16_1_out_8, 1'b0);
  and and_10 (and_10_out, mydecoder4to16_1_out_9, 1'b0);
  and and_11 (and_11_out, mydecoder4to16_1_out_9, 1'b1);
  and and_12 (and_12_out, mydecoder4to16_1_out_10, 1'b1);
  and and_13 (and_13_out, mydecoder4to16_1_out_11, 1'b0);
  or or_2 (or_2_out, and_2_out, and_8_out, and_10_out, and_12_out, and_13_out);
  or or_3 (or_3_out, and_7_out, and_9_out, and_11_out, and_17_out, and_19_out);
  and and_14 (and_14_out, mydecoder4to16_1_out_7, 1'b1);
  and and_15 (and_15_out, mydecoder4to16_1_out_8, 1'b1);
  and and_16 (and_16_out, mydecoder4to16_1_out_9, 1'b0);
  and and_17 (and_17_out, mydecoder4to16_1_out_10, 1'b1);
  and and_18 (and_18_out, mydecoder4to16_1_out_10, 1'b1);
  and and_19 (and_19_out, mydecoder4to16_1_out_11, 1'b0);
  and and_20 (and_20_out, mydecoder4to16_1_out_11, 1'b0);
  or or_4 (or_4_out, and_14_out, and_15_out, and_16_out, and_18_out, and_20_out);
  MyDecoder4To16 mydecoder4to16_1 (
    .in_1(ct[3:0]), .in_2(1'b1), .out_3(mydecoder4to16_1_out_3), .out_4(mydecoder4to16_1_out_4),
    .out_5(mydecoder4to16_1_out_5), .out_6(mydecoder4to16_1_out_6), .out_7(mydecoder4to16_1_out_7),
    .out_8(mydecoder4to16_1_out_8), .out_9(mydecoder4to16_1_out_9), .out_10(mydecoder4to16_1_out_10),
    .out_11(mydecoder4to16_1_out_11), .out_12(mydecoder4to16_1_out_12), .out_13(mydecoder4to16_1_out_13),
    .out_14(mydecoder4to16_1_out_14), .out_15(mydecoder4to16_1_out_15));  // open: out_16, out_17, out_18
  and and_21 (and_21_out, mydecoder4to16_1_out_7, 1'b0);
  and and_22 (and_22_out, mydecoder4to16_1_out_7, 1'b1);
  and and_23 (and_23_out, mydecoder4to16_1_out_8, 1'b1);
  and and_24 (and_24_out, mydecoder4to16_1_out_9, 1'b1);
  and and_25 (and_25_out, mydecoder4to16_1_out_10, 1'b0);
  and and_26 (and_26_out, mydecoder4to16_1_out_11, 1'b0);
  or or_5 (or_5_out, and_21_out, and_23_out, and_24_out, and_25_out, and_26_out);
  and and_27 (and_27_out, mydecoder4to16_1_out_7, 1'b1);
  and and_28 (and_28_out, mydecoder4to16_1_out_8, 1'b0);
  and and_29 (and_29_out, mydecoder4to16_1_out_8, 1'b0);
  and and_30 (and_30_out, mydecoder4to16_1_out_9, 1'b0);
  and and_31 (and_31_out, mydecoder4to16_1_out_9, 1'b0);
  and and_32 (and_32_out, mydecoder4to16_1_out_10, 1'b1);
  and and_33 (and_33_out, mydecoder4to16_1_out_11, 1'b0);
  or or_6 (or_6_out, and_22_out, and_28_out, and_30_out, and_32_out, and_33_out);
  or or_7 (or_7_out, and_27_out, and_29_out, and_31_out, and_37_out, and_39_out);
  and and_34 (and_34_out, mydecoder4to16_1_out_7, 1'b1);
  and and_35 (and_35_out, mydecoder4to16_1_out_8, 1'b0);
  and and_36 (and_36_out, mydecoder4to16_1_out_9, 1'b1);
  and and_37 (and_37_out, mydecoder4to16_1_out_10, 1'b0);
  and and_38 (and_38_out, mydecoder4to16_1_out_10, 1'b1);
  and and_39 (and_39_out, mydecoder4to16_1_out_11, 1'b0);
  and and_40 (and_40_out, mydecoder4to16_1_out_11, 1'b0);
  or or_8 (or_8_out, and_34_out, and_35_out, and_36_out, and_38_out, and_40_out);
  or or_9 (or_9_out, and_44_out, and_43_out, and_42_out, and_41_out);
  and and_41 (and_41_out, 1'b0, mydecoder4to16_1_out_12);
  and and_42 (and_42_out, 1'b1, mydecoder4to16_1_out_13);
  and and_43 (and_43_out, 1'b1, mydecoder4to16_1_out_14);
  and and_44 (and_44_out, 1'b0, mydecoder4to16_1_out_15);
  and and_45 (and_45_out, 1'b1, mydecoder4to16_1_out_15);
  and and_46 (and_46_out, mydecoder4to16_1_out_3, 1'b0);
  and and_47 (and_47_out, mydecoder4to16_1_out_3, 1'b1);
  and and_48 (and_48_out, mydecoder4to16_1_out_4, 1'b1);
  and and_49 (and_49_out, mydecoder4to16_1_out_5, 1'b1);
  and and_50 (and_50_out, mydecoder4to16_1_out_6, 1'b1);
  or or_10 (or_10_out, and_46_out, and_48_out, and_49_out, and_50_out);
  or or_11 (or_11_out, and_45_out, and_54_out, and_52_out, and_51_out);
  or or_12 (or_12_out, and_56_out, and_55_out, and_53_out, and_63_out);
  and and_51 (and_51_out, 1'b1, mydecoder4to16_1_out_12);
  and and_52 (and_52_out, 1'b1, mydecoder4to16_1_out_13);
  and and_53 (and_53_out, 1'b0, mydecoder4to16_1_out_13);
  and and_54 (and_54_out, 1'b1, mydecoder4to16_1_out_14);
  and and_55 (and_55_out, 1'b1, mydecoder4to16_1_out_14);
  and and_56 (and_56_out, 1'b1, mydecoder4to16_1_out_15);
  and and_57 (and_57_out, mydecoder4to16_1_out_3, 1'b0);
  and and_58 (and_58_out, mydecoder4to16_1_out_4, 1'b0);
  and and_59 (and_59_out, mydecoder4to16_1_out_4, 1'b0);
  and and_60 (and_60_out, mydecoder4to16_1_out_5, 1'b0);
  and and_61 (and_61_out, mydecoder4to16_1_out_5, 1'b1);
  and and_62 (and_62_out, mydecoder4to16_1_out_6, 1'b0);
  or or_13 (or_13_out, and_47_out, and_58_out, and_60_out, and_62_out);
  or or_14 (or_14_out, and_57_out, and_59_out, and_61_out, and_71_out);
  or or_15 (or_15_out, and_67_out, and_66_out, and_65_out, and_64_out);
  and and_63 (and_63_out, 1'b1, mydecoder4to16_1_out_12);
  and and_64 (and_64_out, 1'b1, mydecoder4to16_1_out_12);
  and and_65 (and_65_out, 1'b0, mydecoder4to16_1_out_13);
  and and_66 (and_66_out, 1'b1, mydecoder4to16_1_out_14);
  and and_67 (and_67_out, 1'b0, mydecoder4to16_1_out_15);
  and and_68 (and_68_out, mydecoder4to16_1_out_3, 1'b0);
  and and_69 (and_69_out, mydecoder4to16_1_out_4, 1'b1);
  and and_70 (and_70_out, mydecoder4to16_1_out_5, 1'b0);
  and and_71 (and_71_out, mydecoder4to16_1_out_6, 1'b1);
  and and_72 (and_72_out, mydecoder4to16_1_out_6, 1'b1);
  or or_16 (or_16_out, and_68_out, and_69_out, and_70_out, and_72_out);
  or or_17 (or_17_out, and_76_out, and_75_out, and_74_out, and_73_out);
  and and_73 (and_73_out, 1'b0, mydecoder4to16_1_out_12);
  and and_74 (and_74_out, 1'b1, mydecoder4to16_1_out_13);
  and and_75 (and_75_out, 1'b1, mydecoder4to16_1_out_14);
  and and_76 (and_76_out, 1'b1, mydecoder4to16_1_out_15);
  and and_77 (and_77_out, 1'b0, mydecoder4to16_1_out_15);
  and and_78 (and_78_out, mydecoder4to16_1_out_3, 1'b0);
  and and_79 (and_79_out, mydecoder4to16_1_out_3, 1'b0);
  and and_80 (and_80_out, mydecoder4to16_1_out_4, 1'b0);
  and and_81 (and_81_out, mydecoder4to16_1_out_5, 1'b0);
  and and_82 (and_82_out, mydecoder4to16_1_out_6, 1'b0);
  or or_18 (or_18_out, and_78_out, and_80_out, and_81_out, and_82_out);
  or or_19 (or_19_out, and_77_out, and_86_out, and_84_out, and_83_out);
  or or_20 (or_20_out, and_88_out, and_87_out, and_85_out, and_95_out);
  and and_83 (and_83_out, 1'b0, mydecoder4to16_1_out_12);
  and and_84 (and_84_out, 1'b0, mydecoder4to16_1_out_13);
  and and_85 (and_85_out, 1'b1, mydecoder4to16_1_out_13);
  and and_86 (and_86_out, 1'b0, mydecoder4to16_1_out_14);
  and and_87 (and_87_out, 1'b1, mydecoder4to16_1_out_14);
  and and_88 (and_88_out, 1'b0, mydecoder4to16_1_out_15);
  and and_89 (and_89_out, mydecoder4to16_1_out_3, 1'b0);
  and and_90 (and_90_out, mydecoder4to16_1_out_4, 1'b0);
  and and_91 (and_91_out, mydecoder4to16_1_out_4, 1'b0);
  and and_92 (and_92_out, mydecoder4to16_1_out_5, 1'b0);
  and and_93 (and_93_out, mydecoder4to16_1_out_5, 1'b0);
  and and_94 (and_94_out, mydecoder4to16_1_out_6, 1'b0);
  or or_21 (or_21_out, and_79_out, and_90_out, and_92_out, and_94_out);
  or or_22 (or_22_out, and_89_out, and_91_out, and_93_out, and_103_out);
  or or_23 (or_23_out, and_99_out, and_98_out, and_97_out, and_96_out);
  and and_95 (and_95_out, 1'b0, mydecoder4to16_1_out_12);
  and and_96 (and_96_out, 1'b1, mydecoder4to16_1_out_12);
  and and_97 (and_97_out, 1'b1, mydecoder4to16_1_out_13);
  and and_98 (and_98_out, 1'b0, mydecoder4to16_1_out_14);
  and and_99 (and_99_out, 1'b1, mydecoder4to16_1_out_15);
  and and_100 (and_100_out, mydecoder4to16_1_out_3, 1'b0);
  and and_101 (and_101_out, mydecoder4to16_1_out_4, 1'b0);
  and and_102 (and_102_out, mydecoder4to16_1_out_5, 1'b0);
  and and_103 (and_103_out, mydecoder4to16_1_out_6, 1'b0);
  and and_104 (and_104_out, mydecoder4to16_1_out_6, 1'b1);
  or or_24 (or_24_out, and_100_out, and_101_out, and_102_out, and_104_out);
  or or_25 (LSB, or_23_out, or_26_out);
  or or_26 (or_26_out, or_24_out, or_8_out);
  or or_27 (or_27_out, or_22_out, or_7_out);
  or or_28 (or_28_out, or_21_out, or_6_out);
  or or_29 (or_29_out, or_18_out, or_5_out);
  or or_30 (or_30_out, or_16_out, or_4_out);
  or or_31 (or_31_out, or_14_out, or_3_out);
  or or_32 (or_32_out, or_13_out, or_2_out);
  or or_33 (or_33_out, or_10_out, or_1_out);
  or or_34 (out_3, or_20_out, or_27_out);
  or or_35 (out_4, or_19_out, or_28_out);
  or or_36 (out_5, or_17_out, or_29_out);
  or or_37 (out_6, or_15_out, or_30_out);
  or or_38 (out_7, or_12_out, or_31_out);
  or or_39 (out_8, or_11_out, or_32_out);
  or or_40 (MSB, or_9_out, or_33_out);

  // Notes on the sheet:
  //   4. add r1 r1 r3
  //   5.i/o r1 1 000
  //   6. add r2 r2 r1
  //   7. bner0 1101 r1
  //   8. li r0 00 00
  //   10. bner0 0010 r3
  //   11. bner0 1110 r2
  //   12. i/o r2 1 001
  //   9. i/o r3 0 001
  //   0. i/o r0 0 000
  //   1. li r1 00 00
  //   2. li r2 00 00
  //   3. li r3 00 01
endmodule

module sISA (
  input  in_1,
  output [7:0] out_2,
  output [7:0] out_3
);

  wire add, and_5_out, and_6_out, and_16_out, and_23_out, bner0, button_9_out, clock_1_out, device1, device2,
       IO, li, my7segmentdecoder_1_a, my7segmentdecoder_1_b, my7segmentdecoder_1_c, my7segmentdecoder_1_d,
       my7segmentdecoder_1_e, my7segmentdecoder_1_f, my7segmentdecoder_1_g, my7segmentdecoder_2_a,
       my7segmentdecoder_2_b, my7segmentdecoder_2_c, my7segmentdecoder_2_d, my7segmentdecoder_2_e,
       my7segmentdecoder_2_f, my7segmentdecoder_2_g, not_1_out, not_2_out, not_3_out, not_4_out, not_5_out,
       o, or_2_out, or_3_out, s0, s1, s2, s3, xnor_1_out, xnor_2_out, xnor_3_out, xnor_4_out, xnor_5_out,
       xnor_6_out, xnor_7_out, xnor_8_out, y4;
  wire [1:0] addr1, and_7_out, and_10_out, and_12_out, and_14_out, and_17_out, and_19_out, and_20_out,
       b_1_out_8, rd;
  wire [1:1] not_6_out;
  wire [2:0] idx;
  wire [3:0] a_1_data1, a_1_data1_2;
  wire [7:0] a_1_data2, and_2_out, and_4_out, and_21_out, and_22_out, button_8_out, ct_1_pc_out,
       dipswitch_1_sw8, fa8_1_s, fa8_2_s, idx_data, or_4_out;
  wire [7:7] and_1_out, and_3_out, and_18_out;

  not not_1 (not_1_out, o);
  Button button_1 (.out(button_8_out[7]));
  and and_1 (and_1_out[7], device1, IO, not_1_out);
  Button button_2 (.out(button_8_out[4]));
  Button button_3 (.out(button_8_out[5]));
  Button button_4 (.out(button_8_out[6]));
  // Probe on dipswitch_1_sw8
  DipSwitch dipswitch_1 (
    .sw1(dipswitch_1_sw8[7]), .sw2(dipswitch_1_sw8[6]), .sw3(dipswitch_1_sw8[5]), .sw4(dipswitch_1_sw8[4]),
    .sw5(dipswitch_1_sw8[3]), .sw6(dipswitch_1_sw8[2]), .sw7(dipswitch_1_sw8[1]), .sw8(dipswitch_1_sw8[0]));
  not not_2 (not_2_out, o);
  Button button_5 (.out(button_8_out[1]));
  Button button_6 (.out(button_8_out[2]));
  Button button_7 (.out(button_8_out[3]));
  assign and_2_out = {8{and_1_out[7]}} & dipswitch_1_sw8;  // AND_Gate and_2, 8 bits wide
  and and_3 (and_3_out[7], device2, IO, not_2_out);
  Button button_8 (.out(button_8_out[0]));
  assign and_4_out = {8{and_3_out[7]}} & button_8_out;  // AND_Gate and_4, 8 bits wide
  and and_5 (and_5_out, y4, bner0);
  assign idx_data = and_2_out | and_4_out;  // OR_Gate or_1, 8 bits wide
  FA8 fa8_1 (.A(ct_1_pc_out), .B({{5{out_2[7]}}, out_2[2:0]}), .S(fa8_1_s));  // open: Cin, Cout
  // Probe on fa8_1_s
  Button button_9 (.out(button_9_out));
  and and_6 (and_6_out, device2, IO, o);
  // Probe on ct_1_pc_out
  ct ct_1 (.pc_in(fa8_1_s), .clk(or_2_out), .R(button_9_out), .en(and_5_out), .pc_out(ct_1_pc_out));
  MyDecoder2To4 mydecoder2to4_1 (.in_1(b_1_out_8), .out_2(add), .out_3(IO), .out_4(li), .out_5(bner0));
  assign and_7_out = {2{s3}} & idx[1:0];  // AND_Gate and_7, 2 bits wide
  and and_8 (out_2[0], bner0, y4, idx[2]);
  and and_9 (out_2[1], bner0, y4, o);
  assign and_10_out = {2{s2}} & idx[1:0];  // AND_Gate and_10, 2 bits wide
  b b_1 (
    .ct(ct_1_pc_out), .LSB(idx[0]), .out_3(idx[1]), .out_4(idx[2]), .out_5(o), .out_6(rd[0]), .out_7(rd[1]),
    .out_8(b_1_out_8[0]), .MSB(b_1_out_8[1]));
  and and_11 (out_2[2], bner0, y4, rd[0]);
  My7SegmentDecoder my7segmentdecoder_1 (
    .In_1(a_1_data1_2), .in_2(and_6_out), .G(my7segmentdecoder_1_g), .F(my7segmentdecoder_1_f),
    .A(my7segmentdecoder_1_a), .B(my7segmentdecoder_1_b), .E(my7segmentdecoder_1_e),
    .D(my7segmentdecoder_1_d), .C(my7segmentdecoder_1_c));
  My7SegmentDecoder my7segmentdecoder_2 (
    .In_1(a_1_data1), .in_2(and_6_out), .G(my7segmentdecoder_2_g), .F(my7segmentdecoder_2_f),
    .A(my7segmentdecoder_2_a), .B(my7segmentdecoder_2_b), .E(my7segmentdecoder_2_e),
    .D(my7segmentdecoder_2_d), .C(my7segmentdecoder_2_c));
  assign and_12_out = {2{s1}} & idx[1:0];  // AND_Gate and_12, 2 bits wide
  and and_13 (out_2[7], bner0, y4, rd[1]);
  _7_Segment_Display u_7_segment_display_1 (
    .g(my7segmentdecoder_1_g), .f(my7segmentdecoder_1_f), .a(my7segmentdecoder_1_a),
    .b(my7segmentdecoder_1_b), .e(my7segmentdecoder_1_e), .d(my7segmentdecoder_1_d), .c(my7segmentdecoder_1_c));  // open: dp
  assign and_14_out = {2{s0}} & idx[1:0];  // AND_Gate and_14, 2 bits wide
  not not_3 (not_3_out, bner0);
  Clock clock_1 (.out(clock_1_out));
  _7_Segment_Display u_7_segment_display_2 (
    .g(my7segmentdecoder_2_g), .f(my7segmentdecoder_2_f), .a(my7segmentdecoder_2_a),
    .b(my7segmentdecoder_2_b), .e(my7segmentdecoder_2_e), .d(my7segmentdecoder_2_d), .c(my7segmentdecoder_2_c));  // open: dp
  and and_15 (and_17_out[1], o, not_3_out);
  and and_16 (and_16_out, IO, not_4_out);
  not not_4 (not_4_out, o);
  or or_2 (or_2_out, clock_1_out, in_1);
  and and_17 (and_17_out[0], idx[2], not_5_out);
  not not_5 (not_5_out, bner0);
  or or_3 (or_3_out, add, li, and_16_out);
  not not_6 (not_6_out[1], IO);
  // Probe on or_4_out
  // Probe on a_1_data2
  and and_18 (and_18_out[7], device1, o, IO);
  assign and_19_out = {2{IO}} & rd;  // AND_Gate and_19, 2 bits wide
  assign and_20_out = {2{not_6_out[1]}} & and_17_out;  // AND_Gate and_20, 2 bits wide
  // Probe on {and_7_out, and_10_out, and_12_out, and_14_out}
  assign or_4_out = and_22_out | out_3 | idx_data;  // OR_Gate or_4, 8 bits wide
  assign and_21_out = {a_1_data1_2, a_1_data1} & {8{and_18_out[7]}};  // AND_Gate and_21, 8 bits wide
  // LedBar #(.inputtype("row")) ledbar_1: pin names not known; wires that end beside it: and_21_out
  assign addr1 = and_19_out | and_20_out;  // OR_Gate or_5, 2 bits wide
  assign and_22_out = {and_7_out, and_10_out, and_12_out, and_14_out} & {8{li}};  // AND_Gate and_22, 8 bits wide
  MyDecoder2To4 mydecoder2to4_2 (.in_1(and_17_out), .out_2(s0), .out_3(s1), .out_4(s2), .out_5(s3));
  a a_1 (
    .wdata(or_4_out), .clk(or_2_out), .R(button_9_out), .waddr(rd), .EN(or_3_out), .addr1(addr1),
    .addr2(idx[1:0]), .data1({a_1_data1_2, a_1_data1}), .data2(a_1_data2));
  // Probe on a_1_data2
  xnor xnor_1 (xnor_1_out, a_1_data1[0], a_1_data2[0]);
  xnor xnor_2 (xnor_2_out, a_1_data1[1], a_1_data2[1]);
  xnor xnor_3 (xnor_3_out, a_1_data1[2], a_1_data2[2]);
  xnor xnor_4 (xnor_4_out, a_1_data1[3], a_1_data2[3]);
  xnor xnor_5 (xnor_5_out, a_1_data1_2[0], a_1_data2[4]);
  xnor xnor_6 (xnor_6_out, a_1_data1_2[1], a_1_data2[5]);
  xnor xnor_7 (xnor_7_out, a_1_data1_2[2], a_1_data2[6]);
  xnor xnor_8 (xnor_8_out, a_1_data1_2[3], a_1_data2[7]);
  and and_23 (and_23_out, xnor_1_out, xnor_2_out, xnor_3_out, xnor_4_out, xnor_5_out, xnor_6_out, xnor_7_out, xnor_8_out);
  not not_7 (y4, and_23_out);
  MyDecoder3To8 mydecoder3to8_1 (
    .in_1(idx), .Out_8(device1), .Out_7(device2));  // open: Out_6, Out_5, Out_4, Out_3, Out_2, Out_1
  FA8 fa8_2 (.A({a_1_data1_2, a_1_data1}), .B(a_1_data2), .S(fa8_2_s));  // open: Cin, Cout
  and and_24 (out_3[0], fa8_2_s[0], add);
  and and_25 (out_3[1], fa8_2_s[1], add);
  and and_26 (out_3[2], fa8_2_s[2], add);
  and and_27 (out_3[3], fa8_2_s[3], add);
  and and_28 (out_3[4], fa8_2_s[4], add);
  and and_29 (out_3[5], fa8_2_s[5], add);
  and and_30 (out_3[6], fa8_2_s[6], add);
  and and_31 (out_3[7], fa8_2_s[7], add);

  assign out_2[6:3] = {4{out_2[7]}};

  // Other names for the same wires on the sheet: offset[7:0] = {{5{out_2[7]}}, out_2[2:0]}
endmodule

module miniROM (
  input  [31:0] in_1,
  output [31:0] out_2
);

  // Probe on in_1[31:2]
  // Probe on in_1
  // Probe on in_1[5:2]
  Multiplexer #(.select(4), .width(32)) multiplexer_1 (
    .in0(32'h123450b7), .in1(32'h67808093), .in2(32'h1137), .in3(32'h112023), .in4(32'h12183),
    .in5(32'h2137), .in6(32'h420213), .in7(32'h1000a3), .in8(32'h22283), .in9(32'h518333),
    .in10(32'h2c00393), .in11(32'h2c00467), .out(out_2), .sel(in_1[5:2]));  // open: in12, in13, in14, in15
endmodule

module miniRAM (
  input  clk,
  input  [31:0] wdata,
  input  EN,
  input  [4:0] waddr,
  input  [4:0] addr1,
  input  [4:0] addr2,
  output [31:0] data1,
  output [31:0] data2
);

  wire a1, a2, a3, a4, a5, a6, a7, a8, a9, a10, a11, a12, a13, a14, a15, and_1_out, and_2_out, and_3_out,
       and_4_out, and_5_out, and_6_out, and_7_out, and_8_out, and_9_out, and_10_out, and_11_out, and_12_out,
       and_13_out, and_14_out, and_15_out;
  wire [31:0] r0, r1, r2, r3, r4, r5, r6, r7, r8, r9, r10, r11, r12, r13, r14, r15;

  Multiplexer #(.select(5), .width(32)) multiplexer_1 (
    .in0(r0), .in1(r1), .in2(r2), .in3(r3), .in4(r4), .in5(r5), .in6(r6), .in7(r7), .in8(r8), .in9(r9),
    .in10(r10), .in11(r11), .in12(r12), .in13(r13), .in14(r14), .in15(r15), .in16({32{1'b0}}),
    .in17({32{1'b0}}), .in18({32{1'b0}}), .in19({32{1'b0}}), .in20({32{1'b0}}), .in21({32{1'b0}}),
    .in22({32{1'b0}}), .in23({32{1'b0}}), .in24({32{1'b0}}), .in25({32{1'b0}}), .in26({32{1'b0}}),
    .in27({32{1'b0}}), .in28({32{1'b0}}), .in29({32{1'b0}}), .in30({32{1'b0}}), .in31({32{1'b0}}),
    .out(data1), .sel(addr1));
  Multiplexer #(.select(5), .width(32)) multiplexer_2 (
    .in0(r0), .in1(r1), .in2(r2), .in3(r3), .in4(r4), .in5(r5), .in6(r6), .in7(r7), .in8(r8), .in9(r9),
    .in10(r10), .in11(r11), .in12(r12), .in13(r13), .in14(r14), .in15(r15), .in16({32{1'b0}}),
    .in17({32{1'b0}}), .in18({32{1'b0}}), .in19({32{1'b0}}), .in20({32{1'b0}}), .in21({32{1'b0}}),
    .in22({32{1'b0}}), .in23({32{1'b0}}), .in24({32{1'b0}}), .in25({32{1'b0}}), .in26({32{1'b0}}),
    .in27({32{1'b0}}), .in28({32{1'b0}}), .in29({32{1'b0}}), .in30({32{1'b0}}), .in31({32{1'b0}}),
    .out(data2), .sel(addr2));
  Decoder #(.enable("false"), .select(5)) decoder_1 (
    .out1(a1), .out2(a2), .out3(a3), .out4(a4), .out5(a5), .out6(a6), .out7(a7), .out8(a8), .out9(a9),
    .out10(a10), .out11(a11), .out12(a12), .out13(a13), .out14(a14), .out15(a15), .sel(waddr));  // open: out0, out16, out17, out18, out19, out20, out21, out22, out23, out24, out25, out26, out27, out28, out29, out30, out31
  Register #(.width(32)) register_1 (.D(wdata), .en(1'b0), .clk(clk), .Q(r0));  // open: clr
  Register #(.width(32)) register_2 (.D(wdata), .en(and_1_out), .clk(clk), .Q(r8));  // open: clr
  and and_1 (and_1_out, EN, a8);
  Register #(.width(32)) register_3 (.D(wdata), .en(and_2_out), .clk(clk), .Q(r1));  // open: clr
  and and_2 (and_2_out, a1, EN);
  Register #(.width(32)) register_4 (.D(wdata), .en(and_3_out), .clk(clk), .Q(r9));  // open: clr
  and and_3 (and_3_out, EN, a9);
  and and_4 (and_4_out, a2, EN);
  and and_5 (and_5_out, EN, a10);
  Register #(.width(32)) register_5 (.D(wdata), .en(and_4_out), .clk(clk), .Q(r2));  // open: clr
  Register #(.width(32)) register_6 (.D(wdata), .en(and_5_out), .clk(clk), .Q(r10));  // open: clr
  Register #(.width(32)) register_7 (.D(wdata), .en(and_6_out), .clk(clk), .Q(r3));  // open: clr
  and and_6 (and_6_out, a3, EN);
  Register #(.width(32)) register_8 (.D(wdata), .en(and_7_out), .clk(clk), .Q(r11));  // open: clr
  and and_7 (and_7_out, EN, a11);
  Register #(.width(32)) register_9 (.D(wdata), .en(and_8_out), .clk(clk), .Q(r4));  // open: clr
  and and_8 (and_8_out, a4, EN);
  Register #(.width(32)) register_10 (.D(wdata), .en(and_9_out), .clk(clk), .Q(r12));  // open: clr
  and and_9 (and_9_out, EN, a12);
  Register #(.width(32)) register_11 (.D(wdata), .en(and_10_out), .clk(clk), .Q(r5));  // open: clr
  and and_10 (and_10_out, a5, EN);
  Register #(.width(32)) register_12 (.D(wdata), .en(and_11_out), .clk(clk), .Q(r13));  // open: clr
  and and_11 (and_11_out, EN, a13);
  Register #(.width(32)) register_13 (.D(wdata), .en(and_12_out), .clk(clk), .Q(r6));  // open: clr
  and and_12 (and_12_out, a6, EN);
  Register #(.width(32)) register_14 (.D(wdata), .en(and_13_out), .clk(clk), .Q(r14));  // open: clr
  and and_13 (and_13_out, EN, a14);
  Register #(.width(32)) register_15 (.D(wdata), .en(and_14_out), .clk(clk), .Q(r7));  // open: clr
  and and_14 (and_14_out, a7, EN);
  Register #(.width(32)) register_16 (.D(wdata), .en(and_15_out), .clk(clk), .Q(r15));  // open: clr
  and and_15 (and_15_out, EN, a15);
endmodule

module miniPC (
  input  [31:0] w,
  input  clk,
  input  wen,
  output [31:0] out_4
);

  wire [31:0] adder_1_out, multiplexer_1_out, or_1_out;

  Adder #(.width(32)) adder_1 (.a(out_4), .b(32'h4), .out(adder_1_out));  // open: cin, cout
  Multiplexer #(.width(32)) multiplexer_1 (.in0(adder_1_out), .in1({32{1'b0}}), .out(multiplexer_1_out), .sel(wen));
  assign or_1_out = w | multiplexer_1_out;  // OR_Gate or_1, 32 bits wide
  Register #(.width(32)) register_1 (.D(or_1_out), .en(1'b1), .clk(clk), .Q(out_4));  // open: clr
endmodule

module minirv (
  input  in_1,
  input  in_2,
  input  in_3,
  output [63:0] out_4
);

  wire and_1_out, and_3_out, and_5_out, and_7_out, and_8_out, button_1_out, CLK, CLK_IN, comparator_2_eq,
       comparator_3_eq, comparator_4_eq, comparator_8_eq, comparator_9_eq, comparator_10_eq,
       comparator_11_lt, comparator_12_lt, decoder_1_out0, decoder_1_out1, decoder_1_out2, decoder_1_out3,
       isMem, not_1_out, not_2_out, or_2_out, or_3_out, or_4_out, or_5_out, or_6_out, or_7_out, or_8_out,
       or_9_out, rgb_video_1_p3, S;
  wire [1:0] multiplexer_5_out;
  wire [4:0] comparator_7_eq;
  wire [7:0] rgb_video_1_p4, rgb_video_1_p5;
  wire [23:0] multiplexer_5_out_2;
  wire [31:0] adder_1_out, adder_2_out, adder_3_out, adder_4_out, and_6_out, bit_extender_1_out,
       bit_extender_2_out, bit_extender_3_out, bit_extender_4_out, bit_extender_5_out, bit_extender_6_out,
       data2, divider_1_rem, lbu, lbu_d, minipc_1_out_4, miniram_1_data1, multiplexer_2_out,
       multiplexer_3_out, multiplexer_4_out, rom_1_data, subtractor_1_out;
  wire [31:8] divider_1_out, divider_2_out;
  wire [31:26] multiplexer_5_out_3;

  Counter #(.max('hffffffffffffffff), .width(64)) counter_1 (
    .Q(out_4), .clk(CLK), .clr(in_1));  // open: load, D, count, carry, up
  Clock clock_1 (.out(CLK_IN));
  not not_1 (not_1_out, in_2);
  and and_1 (and_1_out, CLK_IN, not_1_out);
  or or_1 (CLK, and_1_out, in_3);
  // Probe on minipc_1_out_4
  miniPC minipc_1 (.w(multiplexer_2_out), .clk(CLK), .wen(comparator_7_eq[0]), .out_4(minipc_1_out_4));
  ROM #(.addrWidth(24), .dataWidth(32)) rom_1 (.addr(minipc_1_out_4[25:2]), .data(rom_1_data));
  Comparator #(.width(32)) comparator_1 (.a(32'h1188), .b(minipc_1_out_4));  // open: gt, eq, lt
  // Probe on minipc_1_out_4[25:2]
  // Probe on rom_1_data
  assign bit_extender_1_out = {{24{1'b0}}, lbu[7:0]};  // Bit_Extender bit_extender_1
  assign bit_extender_2_out = {{24{1'b0}}, lbu[15:8]};  // Bit_Extender bit_extender_2
  assign bit_extender_3_out = {{24{1'b0}}, lbu[23:16]};  // Bit_Extender bit_extender_3
  assign bit_extender_4_out = {{24{1'b0}}, lbu[31:24]};  // Bit_Extender bit_extender_4
  Multiplexer #(.select(2), .width(32)) multiplexer_1 (
    .in0(bit_extender_1_out), .in1(bit_extender_2_out), .in2(bit_extender_3_out), .in3(bit_extender_4_out),
    .out(lbu_d), .sel(multiplexer_5_out));
  Comparator #(.width(3)) comparator_2 (.a(rom_1_data[14:12]), .b(3'b100), .eq(comparator_2_eq));  // open: gt, lt
  Multiplexer #(.width(32)) multiplexer_2 (
    .in0({32{1'b0}}), .in1(and_6_out), .out(multiplexer_2_out), .sel(comparator_7_eq[0]));
  Comparator #(.width(7)) comparator_3 (.a(rom_1_data[6:0]), .b(7'b0100011), .eq(comparator_3_eq));  // open: gt, lt
  Comparator #(.width(7)) comparator_4 (.a(rom_1_data[6:0]), .b(7'b0000011), .eq(comparator_4_eq));  // open: gt, lt
  Comparator #(.width(7)) comparator_5 (.a(rom_1_data[6:0]), .b(7'b0110011), .eq(comparator_7_eq[2]));  // open: gt, lt
  Comparator #(.width(7)) comparator_6 (.a(rom_1_data[6:0]), .b(7'b0110111), .eq(comparator_7_eq[3]));  // open: gt, lt
  Comparator #(.width(7)) comparator_7 (.a(rom_1_data[6:0]), .b(7'b1100111), .eq(comparator_7_eq[0]));  // open: gt, lt
  Comparator #(.width(7)) comparator_8 (.a(rom_1_data[6:0]), .b(7'b0010011), .eq(comparator_8_eq));  // open: gt, lt
  Comparator #(.width(3)) comparator_9 (.a(rom_1_data[14:12]), .b(3'b000), .eq(comparator_9_eq));  // open: gt, lt
  assign bit_extender_5_out = {{20{rom_1_data[31]}}, {rom_1_data[31:25], rom_1_data[11:7]}};  // Bit_Extender bit_extender_5
  Comparator #(.width(3)) comparator_10 (.a(rom_1_data[14:12]), .b(3'b010), .eq(comparator_10_eq));  // open: gt, lt
  and and_2 (comparator_7_eq[4], comparator_2_eq, comparator_4_eq);
  or or_2 (or_2_out, comparator_7_eq[2], comparator_7_eq[0], comparator_8_eq);
  Adder #(.width(32)) adder_1 (.a(32'h4), .b(minipc_1_out_4), .out(adder_1_out));  // open: cin, cout
  and and_3 (and_3_out, comparator_9_eq, comparator_3_eq);
  and sw (S, comparator_3_eq, comparator_10_eq);
  and and_4 (comparator_7_eq[1], comparator_4_eq, comparator_10_eq);
  and and_5 (and_5_out, or_2_out, comparator_9_eq);
  or or_3 (or_3_out, comparator_7_eq[4], comparator_7_eq[1], comparator_7_eq[3], and_5_out);
  assign bit_extender_6_out = {{20{rom_1_data[31]}}, rom_1_data[31:20]};  // Bit_Extender bit_extender_6
  or or_4 (or_4_out, and_3_out, S);
  Multiplexer #(.select(5), .width(32)) multiplexer_3 (
    .in0(adder_2_out), .in1(adder_1_out), .in2(lbu), .in4(adder_3_out),
    .in8({rom_1_data[31:12], {12{1'b0}}}), .in16(lbu_d), .out(multiplexer_3_out));  // open: in3, in5, in6, in7, in9, in10, in11, in12, in13, in14, in15, in17, in18, in19, in20, in21, in22, in23, in24, in25, in26, in27, in28, in29, in30, in31, sel
  or or_5 (or_5_out, S, decoder_1_out3);
  or or_6 (or_6_out, S, decoder_1_out2);
  or or_7 (or_7_out, S, decoder_1_out1);
  or or_8 (or_8_out, S, decoder_1_out0);
  Multiplexer #(.width(32)) multiplexer_4 (
    .in0(data2), .in1({data2[7:0], data2[7:0], data2[7:0], data2[7:0]}), .out(multiplexer_4_out),
    .sel(and_3_out));
  assign and_6_out = 32'hfffffffe & adder_2_out;  // AND_Gate and_6, 32 bits wide
  miniRAM miniram_1 (
    .clk(CLK), .wdata(multiplexer_3_out), .EN(or_3_out), .waddr(rom_1_data[11:7]), .addr1(rom_1_data[19:15]),
    .addr2(rom_1_data[24:20]), .data1(miniram_1_data1), .data2(data2));
  and and_7 (and_7_out, isMem, or_4_out);
  RAM #(.addrWidth(24), .asyncread("true"), .byteenables("byteEnables"), .dataWidth(32), .\type ("nonvolatile")) ram_1 (
    .addr(multiplexer_5_out_2), .we(and_7_out), .oe(1'b1), .clk(CLK), .din(multiplexer_4_out), .dout(lbu),
    .be3(or_5_out), .be2(or_6_out), .be1(or_7_out), .be0(or_8_out));
  Decoder #(.enable("false"), .select(2)) decoder_1 (
    .out0(decoder_1_out0), .out1(decoder_1_out1), .out2(decoder_1_out2), .out3(decoder_1_out3),
    .sel(multiplexer_5_out));
  // Probe on lbu_d
  Adder #(.width(32)) adder_2 (.a(miniram_1_data1), .b(bit_extender_6_out), .out(adder_2_out));  // open: cin, cout
  Adder #(.width(32)) adder_3 (.a(miniram_1_data1), .b(data2), .out(adder_3_out));  // open: cin, cout
  Adder #(.width(32)) adder_4 (.a(miniram_1_data1), .b(bit_extender_5_out), .out(adder_4_out));  // open: cin, cout
  Button button_1 (.out(button_1_out));
  or or_9 (or_9_out, and_3_out, S);
  Multiplexer #(.width(32)) multiplexer_5 (
    .in0(adder_2_out), .in1(adder_4_out),
    .out({multiplexer_5_out_3, multiplexer_5_out_2, multiplexer_5_out}), .sel(or_9_out));
  // RGB_Video #(.cursor("No Cursor"), .height(256), .width(256)) rgb_video_1: pin names not known; wires that end beside it: button_1_out, CLK, rgb_video_1_p3, rgb_video_1_p4, rgb_video_1_p5, data2[23:0]
  Comparator #(.width(32)) comparator_11 (
    .a({multiplexer_5_out_3, multiplexer_5_out_2, multiplexer_5_out}), .b(32'h20040000), .lt(comparator_11_lt));  // open: gt, eq
  Comparator #(.width(32)) comparator_12 (
    .a({multiplexer_5_out_3, multiplexer_5_out_2, multiplexer_5_out}), .b(32'h20000000), .lt(comparator_12_lt));  // open: gt, eq
  not not_2 (not_2_out, comparator_12_lt);
  and and_8 (and_8_out, comparator_11_lt, not_2_out);
  and and_9 (rgb_video_1_p3, S, and_8_out);
  not not_3 (isMem, and_8_out);
  // Probe on nothing
  Subtractor #(.width(32)) subtractor_1 (
    .a({multiplexer_5_out_3, multiplexer_5_out_2, multiplexer_5_out}), .b(32'h20000000),
    .out(subtractor_1_out));  // open: bin, bout
  Divider #(.width(32)) divider_1 (
    .a(subtractor_1_out), .b(32'h400), .out({divider_1_out, rgb_video_1_p5}), .rem(divider_1_rem));  // open: upper
  Divider #(.width(32)) divider_2 (
    .a(divider_1_rem), .b(32'h4), .out({divider_2_out, rgb_video_1_p4}));  // open: upper, rem

  // Other names for the same wires on the sheet: CMP = in_2; rgb[23:0] = data2[23:0];
  //   sb[31:0] = {data2[7:0], data2[7:0], data2[7:0], data2[7:0]}

  // Notes on the sheet:
  //   contents of rom_1 (hex, n*v repeats v):
  //   413 52137 10113 10b7 22408093 80e7 fea12823 fe812e23 1437 40840413 ff014183 3401b3 1c183 ff114203
  //   440233 24203 4181b3 ff214203 440233 24203 4181b3 ff314203 440233 24203 4181b3 1237 40020213 320233
  //   24203 ffc12403 420233 420233 410233 a000193 fe312823 9c00193 fe312623 fec22203 20067 8067 ff410113
  //   100513 112423 10b7 21808093 80e7 fec10113 912423 494b7 6b048493 812623 112823 496b7 69068693 48413
  //   48713 fe012823 174183 fe3109a3 ff012183 fe812e23 fe312823 3d437 60040413 ff214203 420233 420233
  //   440233 22203 fe412623 ff114203 420233 420233 440233 22203 fe412423 ff014203 420233 420233 440233
  //   22203 fe412223 fed14183 fea14203 4181b3 fe714203 4181b3 fe312223 fee14183 feb14203 4181b3 fe3102a3
  //   fef14183 fe310323 fe412183 8237 20213 440433 ff314203 420233 420233 440233 22203 ffc12403 4181b3
  //   74503 350533 6a603 270713 468693 fe312a23 fec12423 31237 50020213 feb14183 4181b3 1c183 fe3103a3
  //   fea14183 4181b3 1c183 fe310323 fe914183 4181b3 1c183 fe3102a3 fe814183 4181b3 1c183 fe310223
  //   ff412183 fe412203 450533 150513 fea12823 fe812e23 1437 40840413 ff014183 3401b3 1c183 ff114203
  //   440233 24203 4181b3 ff214203 440233 24203 4181b3 ff314203 440233 24203 4181b3 1237 40020213 320233
  //   24503 ffc12403 e12223 d12023 1800093 80e7 412703 497b7 6c078793 12683 fee12823 fef12623 fe812e23
  //   fe912c23 1437 30040413 ff014183 340233 100193 320023 fec14183 3401b3 18023 24183 ff114483 940233
  //   100493 920023 fed14483 9404b3 48023 24483 9181b3 ff214483 940233 100493 920023 fee14483 9404b3 48023
  //   24483 9181b3 ff314483 940233 100493 920023 fef14483 9404b3 48023 24483 9181b3 1237 40020213 320233
  //   24203 ff812483 ffc12403 420233 420233 410233 37800193 fe312823 e000193 fe312623 fec22203 20067 49737
  //   67070713 72683 fe012823 14c203 fe4108a3 ff012203 4c503 450533 470713 e12023 fe312a23 fed12423 31237
  //   50020213 feb14183 4181b3 1c183 fe3103a3 fea14183 4181b3 1c183 fe310323 fe914183 4181b3 1c183
  //   fe3102a3 fe814183 4181b3 1c183 fe310223 ff412183 fe412203 450533 150513 fea12823 fe812e23 1437
  //   40840413 ff014183 3401b3 1c183 ff114203 440233 24203 4181b3 ff214203 440233 24203 4181b3 ff314203
  //   440233 24203 4181b3 1237 40020213 320233 24503 ffc12403 1800093 80e7 248493 497b7 6c078793 12703
  //   fe912823 fef12623 fe812e23 fe912c23 1437 30040413 ff014183 340233 100193 320023 fec14183 3401b3
  //   18023 24183 ff114483 940233 100493 920023 fed14483 9404b3 48023 24483 9181b3 ff214483 940233 100493
  //   920023 fee14483 9404b3 48023 24483 9181b3 ff314483 940233 100493 920023 fef14483 9404b3 48023 24483
  //   9181b3 1237 40020213 320233 24203 ff812483 ffc12403 420233 420233 410233 55c00193 fe312823 38000193
  //   fe312623 fec22203 20067 244683 144603 344703 444783 494b7 64048493 8*d686b3 fed12823 fec12623 116b7
  //   60068693 fe012223 ff314203 fe4102a3 fef14203 fe410223 fe412203 468233 24203 fe4105a3 ff214203
  //   fe4102a3 fee14203 fe410223 fe412203 468233 24203 fe410523 ff114203 fe4102a3 fed14203 fe410223
  //   fe412203 468233 24203 fe4104a3 ff014203 fe4102a3 fec14203 fe410223 fe412203 468233 24203 fe410423
  //   fe812683 4a503 fe012823 fee10923 fee12423 fe914203 fe4109a3 ff012703 fee12823 fed12623 11737
  //   60070713 fe012223 ff314203 fe4102a3 fef14203 fe410223 fe412203 470233 24203 fe4105a3 ff214203
  //   fe4102a3 fee14203 fe410223 fe412203 470233 24203 fe410523 ff114203 fe4102a3 fed14203 fe410223
  //   fe412203 470233 24203 fe4104a3 ff014203 fe4102a3 fec14203 fe410223 fe412203 470233 24203 fe410423
  //   fe812703 fe012823 fef109a3 ff012783 fef12823 fee12623 117b7 60078793 fe012223 ff314203 fe4102a3
  //   fef14203 fe410223 fe412203 478233 24203 fe4105a3 ff214203 fe4102a3 fee14203 fe410223 fe412203 478233
  //   24203 fe410523 ff114203 fe4102a3 fed14203 fe410223 fe412203 478233 24203 fe4104a3 ff014203 fe4102a3
  //   fec14203 fe410223 fe412203 478233 24203 fe410423 fe812783 fe312a23 fef12423 31237 50020213 feb14183
  //   4181b3 1c183 fe3103a3 fea14183 4181b3 1c183 fe310323 fe914183 4181b3 1c183 fe3102a3 fe814183 4181b3
  //   1c183 fe310223 ff412183 fe412203 450533 150513 fea12823 fe812e23 1437 40840413 ff014183 3401b3 1c183
  //   ff114203 440233 24203 4181b3 ff214203 440233 24203 4181b3 ff314203 440233 24203 4181b3 1237 400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
  //   lbu  0extend
  //   lui imm<<12
  //   sb/sw sign extend
  //   jalr PC+4
  //   lw/lbu/addi sign extend
  //   jalr  jump to (rs1+imm)&fffffffe
  //   lw/lbu/addi
  //   add
  //   sw sb
  //   sw/sb
  //   0~256  8bit
  //   lbu/sb address
  //   lw/sw (rs1 + imm)
  //   RGB's EN
  //   A line 4*256 = 1024 = 0x400
  //   address-20000000
  //   Y
  //   X
endmodule

module my_NAND (
  input  in_1,
  input  in_2,
  output out_3,
  output out_4
);

  wire transistor_1_out;

  Transistor #(.\type ("n")) transistor_1 (.in(1'b0), .out(transistor_1_out), .gate(in_2));
  Transistor #(.\type ("n")) transistor_2 (.in(transistor_1_out), .out(out_4), .gate(in_1));
  Transistor transistor_3 (.in(1'b1), .out(out_4), .gate(in_1));
  Transistor transistor_4 (.in(1'b1), .out(out_4), .gate(in_2));
  nand nand_1 (out_3, in_2, in_1);
endmodule

module OAI22X1H7L (
  input  A0,
  input  A1,
  input  B0,
  input  B1,
  output Y
);

  wire transistor_1_out, transistor_2_out, transistor_5_out;

  Transistor transistor_1 (.in(1'b1), .out(transistor_1_out), .gate(B0));
  Transistor #(.\type ("n")) transistor_2 (.in(1'b0), .out(transistor_2_out), .gate(A0));
  Transistor #(.\type ("n")) transistor_3 (.in(1'b0), .out(transistor_2_out), .gate(A1));
  Transistor transistor_4 (.in(transistor_1_out), .out(Y), .gate(B1));
  Transistor transistor_5 (.in(1'b1), .out(transistor_5_out), .gate(A0));
  Transistor transistor_6 (.in(transistor_5_out), .out(Y), .gate(A1));
  Transistor #(.\type ("n")) transistor_7 (.in(transistor_2_out), .out(Y), .gate(B0));
  Transistor #(.\type ("n")) transistor_8 (.in(transistor_2_out), .out(Y), .gate(B1));
endmodule
